// Logisim project MIPS.circ as structural Verilog: 27 circuits, main circuit MIPS_V01
module MIPS_V01 (
  input  FREEZE_IN,
  input  RESET_IN,
  output IF_ERROR,
  output ALU_OVERFLOW,
  output ADDR_ERR_OUT
);

  wire ERR_q, exe_stage_1_j_b_out, MAIN_CLOCK_out, mem_bank_mem_wb_1_load_opc_out, mem_stage_1_load_opc_out,
       or_1_out;
  wire [1:0] CAUSE_q, or_2_out;
  wire [4:0] dec_stage_1_rd_out, dec_stage_1_rs_out, dec_stage_1_rt_out, dec_stage_1_shift_out,
       exe_stage_1_rd_out, exe_stage_1_rs_out, exe_stage_1_rt_out, mem_bank_dec_exe_1_rd_out,
       mem_bank_dec_exe_1_rs_out, mem_bank_dec_exe_1_rt_out, mem_bank_dec_exe_1_shift_out,
       mem_bank_exe_mem_1_rd_out, mem_bank_exe_mem_1_rs_out, mem_bank_exe_mem_1_rt_out,
       mem_bank_mem_wb_1_rd_out, mem_bank_mem_wb_1_rs_out, mem_bank_mem_wb_1_rt_out, mem_stage_1_rd_out,
       mem_stage_1_rs_out, mem_stage_1_rt_out, wb_stage_1_data_addr_out;
  wire [5:0] dec_stage_1_func_out, dec_stage_1_opc_out, exe_stage_1_opc_out, mem_bank_dec_exe_1_func_out,
       mem_bank_dec_exe_1_opc_out, mem_bank_exe_mem_1_opc_out, mem_bank_mem_wb_1_opc_out, mem_stage_1_opc_out;
  wire [15:0] dec_stage_1_imm_out, mem_bank_dec_exe_1_imm_out;
  wire [23:0] dec_stage_1_pc_out, exe_stage_1_pc_addr_out, exe_stage_1_pc_out, if_stage_1_pc_out,
       mem_bank_dec_exe_1_pc_out, mem_bank_exe_mem_1_pc_out, mem_bank_if_dec_1_pc_out,
       mem_bank_mem_wb_1_pc_out, mem_stage_1_pc_out;
  wire [31:0] dec_stage_1_vrs_out, dec_stage_1_vrt_out, exe_stage_1_alu_out, exe_stage_1_vrt_out,
       if_stage_1_instruction_out, mem_bank_dec_exe_1_vrs_out, mem_bank_dec_exe_1_vrt_out,
       mem_bank_exe_mem_1_vrd_out, mem_bank_exe_mem_1_vrt_out, mem_bank_if_dec_1_instruction_out,
       mem_bank_mem_wb_1_data_out, mem_bank_mem_wb_1_vrd_out, mem_stage_1_data_out, mem_stage_1_vrd_out,
       wb_stage_1_data_out;

  Clock MAIN_CLOCK (.out(MAIN_CLOCK_out));
  IF_STAGE if_stage_1 (
    .INST_ADDR_OVERFLOW_OUT(IF_ERROR), .NEXT_PC_IN(exe_stage_1_pc_addr_out), .J_B_IN(exe_stage_1_j_b_out),
    .FREEZE_IN(FREEZE_IN), .CLOCK_IN(MAIN_CLOCK_out), .RESET_IN(RESET_IN), .PC_OUT(if_stage_1_pc_out),
    .INSTRUCTION_OUT(if_stage_1_instruction_out));
  MEM_BANK_IF_DEC mem_bank_if_dec_1 (
    .PC_IN(if_stage_1_pc_out), .INSTRUCTION_IN(if_stage_1_instruction_out), .FREEZE_IN(FREEZE_IN),
    .CLOCK_IN(MAIN_CLOCK_out), .RESET_IN(RESET_IN), .PC_OUT(mem_bank_if_dec_1_pc_out),
    .INSTRUCTION_OUT(mem_bank_if_dec_1_instruction_out));
  DEC_STAGE dec_stage_1 (
    .PC_IN(mem_bank_if_dec_1_pc_out), .INSTRUCTION_IN(mem_bank_if_dec_1_instruction_out),
    .FREEZE_IN(FREEZE_IN), .CLOCK_IN(MAIN_CLOCK_out), .RESET_IN(RESET_IN),
    .WRITE_DATA_IN(wb_stage_1_data_out), .REG_ADDR_IN(wb_stage_1_data_addr_out), .PC_OUT(dec_stage_1_pc_out),
    .OPC_OUT(dec_stage_1_opc_out), .FUNC_OUT(dec_stage_1_func_out), .RS_OUT(dec_stage_1_rs_out),
    .RT_OUT(dec_stage_1_rt_out), .RD_OUT(dec_stage_1_rd_out), .SHIFT_OUT(dec_stage_1_shift_out),
    .IMM_OUT(dec_stage_1_imm_out), .VRS_OUT(dec_stage_1_vrs_out), .VRT_OUT(dec_stage_1_vrt_out));
  MEM_BANK_DEC_EXE mem_bank_dec_exe_1 (
    .PC_IN(dec_stage_1_pc_out), .OPC_IN(dec_stage_1_opc_out), .FUNC_IN(dec_stage_1_func_out),
    .RS_IN(dec_stage_1_rs_out), .RT_IN(dec_stage_1_rt_out), .RD_IN(dec_stage_1_rd_out),
    .SHIFT_IN(dec_stage_1_shift_out), .IMM_IN(dec_stage_1_imm_out), .VRS_IN(dec_stage_1_vrs_out),
    .VRT_IN(dec_stage_1_vrt_out), .FREEZE_IN(FREEZE_IN), .CLOCK_IN(MAIN_CLOCK_out), .RESET_IN(RESET_IN),
    .PC_OUT(mem_bank_dec_exe_1_pc_out), .OPC_OUT(mem_bank_dec_exe_1_opc_out),
    .FUNC_OUT(mem_bank_dec_exe_1_func_out), .RS_OUT(mem_bank_dec_exe_1_rs_out),
    .RT_OUT(mem_bank_dec_exe_1_rt_out), .RD_OUT(mem_bank_dec_exe_1_rd_out),
    .SHIFT_OUT(mem_bank_dec_exe_1_shift_out), .IMM_OUT(mem_bank_dec_exe_1_imm_out),
    .VRS_OUT(mem_bank_dec_exe_1_vrs_out), .VRT_OUT(mem_bank_dec_exe_1_vrt_out));
  EXE_STAGE exe_stage_1 (
    .PC_IN(mem_bank_dec_exe_1_pc_out), .OPC_IN(mem_bank_dec_exe_1_opc_out),
    .FUNC_IN(mem_bank_dec_exe_1_func_out), .RS_IN(mem_bank_dec_exe_1_rs_out),
    .RT_IN(mem_bank_dec_exe_1_rt_out), .RD_IN(mem_bank_dec_exe_1_rd_out),
    .SHIFT_IN(mem_bank_dec_exe_1_shift_out), .IMM_IN(mem_bank_dec_exe_1_imm_out),
    .VRS_IN(mem_bank_dec_exe_1_vrs_out), .VRT_IN(mem_bank_dec_exe_1_vrt_out),
    .ALU_OVERFLOW_OUT(ALU_OVERFLOW), .J_B_OUT(exe_stage_1_j_b_out), .PC_ADDR_OUT(exe_stage_1_pc_addr_out),
    .FREEZE_IN(FREEZE_IN), .CLOCK_IN(MAIN_CLOCK_out), .RESET_IN(RESET_IN), .PC_OUT(exe_stage_1_pc_out),
    .OPC_OUT(exe_stage_1_opc_out), .RS_OUT(exe_stage_1_rs_out), .RT_OUT(exe_stage_1_rt_out),
    .RD_OUT(exe_stage_1_rd_out), .ALU_OUT(exe_stage_1_alu_out), .VRT_OUT(exe_stage_1_vrt_out));
  MEM_BANK_EXE_MEM mem_bank_exe_mem_1 (
    .PC_IN(exe_stage_1_pc_out), .OPC_IN(exe_stage_1_opc_out), .RS_IN(exe_stage_1_rs_out),
    .RT_IN(exe_stage_1_rt_out), .RD_IN(exe_stage_1_rd_out), .ALU_IN(exe_stage_1_alu_out),
    .VRT_IN(exe_stage_1_vrt_out), .FREEZE_IN(FREEZE_IN), .CLOCK_IN(MAIN_CLOCK_out), .RESET_IN(RESET_IN),
    .VRD_OUT(mem_bank_exe_mem_1_vrd_out), .VRT_OUT(mem_bank_exe_mem_1_vrt_out),
    .PC_OUT(mem_bank_exe_mem_1_pc_out), .OPC_OUT(mem_bank_exe_mem_1_opc_out),
    .RS_OUT(mem_bank_exe_mem_1_rs_out), .RT_OUT(mem_bank_exe_mem_1_rt_out), .RD_OUT(mem_bank_exe_mem_1_rd_out));
  MEM_STAGE mem_stage_1 (
    .VRD_IN(mem_bank_exe_mem_1_vrd_out), .VRT_IN(mem_bank_exe_mem_1_vrt_out),
    .PC_IN(mem_bank_exe_mem_1_pc_out), .OPC_IN(mem_bank_exe_mem_1_opc_out),
    .RS_IN(mem_bank_exe_mem_1_rs_out), .RT_IN(mem_bank_exe_mem_1_rt_out), .RD_IN(mem_bank_exe_mem_1_rd_out),
    .ADDR_ERR_OUT(ADDR_ERR_OUT), .FREEZE_IN(FREEZE_IN), .CLOCK_IN(MAIN_CLOCK_out), .RESET_IN(RESET_IN),
    .VRD_OUT(mem_stage_1_vrd_out), .PC_OUT(mem_stage_1_pc_out), .OPC_OUT(mem_stage_1_opc_out),
    .DATA_OUT(mem_stage_1_data_out), .LOAD_OPC_OUT(mem_stage_1_load_opc_out), .RS_OUT(mem_stage_1_rs_out),
    .RT_OUT(mem_stage_1_rt_out), .RD_OUT(mem_stage_1_rd_out));
  MEM_BANK_MEM_WB mem_bank_mem_wb_1 (
    .VRD_IN(mem_stage_1_vrd_out), .PC_IN(mem_stage_1_pc_out), .OPC_IN(mem_stage_1_opc_out),
    .DATA_IN(mem_stage_1_data_out), .LOAD_OPC_IN(mem_stage_1_load_opc_out), .RS_IN(mem_stage_1_rs_out),
    .RT_IN(mem_stage_1_rt_out), .RD_IN(mem_stage_1_rd_out), .FREEZE_IN(FREEZE_IN), .CLOCK_IN(MAIN_CLOCK_out),
    .RESET_IN(RESET_IN), .VRD_OUT(mem_bank_mem_wb_1_vrd_out), .PC_OUT(mem_bank_mem_wb_1_pc_out),
    .OPC_OUT(mem_bank_mem_wb_1_opc_out), .DATA_OUT(mem_bank_mem_wb_1_data_out),
    .LOAD_OPC_OUT(mem_bank_mem_wb_1_load_opc_out), .RS_OUT(mem_bank_mem_wb_1_rs_out),
    .RT_OUT(mem_bank_mem_wb_1_rt_out), .RD_OUT(mem_bank_mem_wb_1_rd_out));
  WB_STAGE wb_stage_1 (
    .VRD_IN(mem_bank_mem_wb_1_vrd_out), .PC_IN(mem_bank_mem_wb_1_pc_out), .OPC_IN(mem_bank_mem_wb_1_opc_out),
    .DATA_IN(mem_bank_mem_wb_1_data_out), .LOAD_OPC_IN(mem_bank_mem_wb_1_load_opc_out),
    .RS_IN(mem_bank_mem_wb_1_rs_out), .RT_IN(mem_bank_mem_wb_1_rt_out), .RD_IN(mem_bank_mem_wb_1_rd_out),
    .FREEZE_IN(FREEZE_IN), .CLOCK_IN(MAIN_CLOCK_out), .RESET_IN(RESET_IN), .DATA_OUT(wb_stage_1_data_out),
    .DATA_ADDR_OUT(wb_stage_1_data_addr_out));
  or or_1 (or_1_out, IF_ERROR, ALU_OVERFLOW, ADDR_ERR_OUT);
  Register #(.width(1)) ERR (.D(or_1_out), .en(or_1_out), .Q(ERR_q), .clk(MAIN_CLOCK_out), .clr(RESET_IN));
  or or_2 (or_2_out[0], IF_ERROR, ADDR_ERR_OUT);
  or or_3 (or_2_out[1], ALU_OVERFLOW, ADDR_ERR_OUT);
  Register #(.width(2)) CAUSE (.D(or_2_out), .en(or_1_out), .Q(CAUSE_q), .clk(MAIN_CLOCK_out), .clr(RESET_IN));
endmodule

module _1BIT_ADD (
  input  A_IN,
  input  B_IN,
  input  CARRY_IN,
  output VAL_OUT,
  output CARRY_OUT
);

  wire and_1_out, and_2_out, xor_1_out;

  xor xor_1 (xor_1_out, A_IN, B_IN);
  and and_1 (and_1_out, A_IN, B_IN);
  and and_2 (and_2_out, xor_1_out, CARRY_IN);
  xor xor_2 (VAL_OUT, xor_1_out, CARRY_IN);
  or or_1 (CARRY_OUT, and_1_out, and_2_out);
endmodule

module _32BITS_INC (
  input  [31:0] DATA_IN,
  output [31:0] DATA_OUT,
  output OVERFLOW_OUT
);

  wire n1bit_add_1_carry_out, n1bit_add_2_carry_out, n1bit_add_3_carry_out, n1bit_add_4_carry_out,
       n1bit_add_5_carry_out, n1bit_add_6_carry_out, n1bit_add_7_carry_out, n1bit_add_8_carry_out,
       n1bit_add_9_carry_out, n1bit_add_10_carry_out, n1bit_add_11_carry_out, n1bit_add_12_carry_out,
       n1bit_add_13_carry_out, n1bit_add_14_carry_out, n1bit_add_15_carry_out, n1bit_add_17_carry_out,
       n1bit_add_18_carry_out, n1bit_add_19_carry_out, n1bit_add_20_carry_out, n1bit_add_21_carry_out,
       n1bit_add_22_carry_out, n1bit_add_23_carry_out, n1bit_add_24_carry_out, n1bit_add_25_carry_out,
       n1bit_add_26_carry_out, n1bit_add_27_carry_out, n1bit_add_28_carry_out, n1bit_add_29_carry_out,
       n1bit_add_30_carry_out, n1bit_add_31_carry_out, n1bit_add_32_carry_out;

  _1BIT_ADD u_1bit_add_1 (
    .A_IN(n1bit_add_17_carry_out), .B_IN(DATA_IN[1]), .CARRY_IN(1'b0), .VAL_OUT(DATA_OUT[1]),
    .CARRY_OUT(n1bit_add_1_carry_out));
  _1BIT_ADD u_1bit_add_2 (
    .A_IN(n1bit_add_18_carry_out), .B_IN(DATA_IN[3]), .CARRY_IN(1'b0), .VAL_OUT(DATA_OUT[3]),
    .CARRY_OUT(n1bit_add_2_carry_out));
  _1BIT_ADD u_1bit_add_3 (
    .A_IN(n1bit_add_19_carry_out), .B_IN(DATA_IN[5]), .CARRY_IN(1'b0), .VAL_OUT(DATA_OUT[5]),
    .CARRY_OUT(n1bit_add_3_carry_out));
  _1BIT_ADD u_1bit_add_4 (
    .A_IN(n1bit_add_20_carry_out), .B_IN(DATA_IN[7]), .CARRY_IN(1'b0), .VAL_OUT(DATA_OUT[7]),
    .CARRY_OUT(n1bit_add_4_carry_out));
  _1BIT_ADD u_1bit_add_5 (
    .A_IN(n1bit_add_21_carry_out), .B_IN(DATA_IN[9]), .CARRY_IN(1'b0), .VAL_OUT(DATA_OUT[9]),
    .CARRY_OUT(n1bit_add_5_carry_out));
  _1BIT_ADD u_1bit_add_6 (
    .A_IN(n1bit_add_22_carry_out), .B_IN(DATA_IN[11]), .CARRY_IN(1'b0), .VAL_OUT(DATA_OUT[11]),
    .CARRY_OUT(n1bit_add_6_carry_out));
  _1BIT_ADD u_1bit_add_7 (
    .A_IN(n1bit_add_23_carry_out), .B_IN(DATA_IN[13]), .CARRY_IN(1'b0), .VAL_OUT(DATA_OUT[13]),
    .CARRY_OUT(n1bit_add_7_carry_out));
  _1BIT_ADD u_1bit_add_8 (
    .A_IN(n1bit_add_24_carry_out), .B_IN(DATA_IN[15]), .CARRY_IN(1'b0), .VAL_OUT(DATA_OUT[15]),
    .CARRY_OUT(n1bit_add_8_carry_out));
  _1BIT_ADD u_1bit_add_9 (
    .A_IN(n1bit_add_25_carry_out), .B_IN(DATA_IN[17]), .CARRY_IN(1'b0), .VAL_OUT(DATA_OUT[17]),
    .CARRY_OUT(n1bit_add_9_carry_out));
  _1BIT_ADD u_1bit_add_10 (
    .A_IN(n1bit_add_26_carry_out), .B_IN(DATA_IN[19]), .CARRY_IN(1'b0), .VAL_OUT(DATA_OUT[19]),
    .CARRY_OUT(n1bit_add_10_carry_out));
  _1BIT_ADD u_1bit_add_11 (
    .A_IN(n1bit_add_27_carry_out), .B_IN(DATA_IN[21]), .CARRY_IN(1'b0), .VAL_OUT(DATA_OUT[21]),
    .CARRY_OUT(n1bit_add_11_carry_out));
  _1BIT_ADD u_1bit_add_12 (
    .A_IN(n1bit_add_28_carry_out), .B_IN(DATA_IN[23]), .CARRY_IN(1'b0), .VAL_OUT(DATA_OUT[23]),
    .CARRY_OUT(n1bit_add_12_carry_out));
  _1BIT_ADD u_1bit_add_13 (
    .A_IN(n1bit_add_29_carry_out), .B_IN(DATA_IN[25]), .CARRY_IN(1'b0), .VAL_OUT(DATA_OUT[25]),
    .CARRY_OUT(n1bit_add_13_carry_out));
  _1BIT_ADD u_1bit_add_14 (
    .A_IN(n1bit_add_30_carry_out), .B_IN(DATA_IN[27]), .CARRY_IN(1'b0), .VAL_OUT(DATA_OUT[27]),
    .CARRY_OUT(n1bit_add_14_carry_out));
  _1BIT_ADD u_1bit_add_15 (
    .A_IN(n1bit_add_31_carry_out), .B_IN(DATA_IN[29]), .CARRY_IN(1'b0), .VAL_OUT(DATA_OUT[29]),
    .CARRY_OUT(n1bit_add_15_carry_out));
  _1BIT_ADD u_1bit_add_16 (
    .A_IN(n1bit_add_32_carry_out), .B_IN(DATA_IN[31]), .CARRY_IN(1'b0), .VAL_OUT(DATA_OUT[31]),
    .CARRY_OUT(OVERFLOW_OUT));
  _1BIT_ADD u_1bit_add_17 (
    .A_IN(1'b1), .B_IN(DATA_IN[0]), .CARRY_IN(1'b0), .VAL_OUT(DATA_OUT[0]), .CARRY_OUT(n1bit_add_17_carry_out));
  _1BIT_ADD u_1bit_add_18 (
    .A_IN(n1bit_add_1_carry_out), .B_IN(DATA_IN[2]), .CARRY_IN(1'b0), .VAL_OUT(DATA_OUT[2]),
    .CARRY_OUT(n1bit_add_18_carry_out));
  _1BIT_ADD u_1bit_add_19 (
    .A_IN(n1bit_add_2_carry_out), .B_IN(DATA_IN[4]), .CARRY_IN(1'b0), .VAL_OUT(DATA_OUT[4]),
    .CARRY_OUT(n1bit_add_19_carry_out));
  _1BIT_ADD u_1bit_add_20 (
    .A_IN(n1bit_add_3_carry_out), .B_IN(DATA_IN[6]), .CARRY_IN(1'b0), .VAL_OUT(DATA_OUT[6]),
    .CARRY_OUT(n1bit_add_20_carry_out));
  _1BIT_ADD u_1bit_add_21 (
    .A_IN(n1bit_add_4_carry_out), .B_IN(DATA_IN[8]), .CARRY_IN(1'b0), .VAL_OUT(DATA_OUT[8]),
    .CARRY_OUT(n1bit_add_21_carry_out));
  _1BIT_ADD u_1bit_add_22 (
    .A_IN(n1bit_add_5_carry_out), .B_IN(DATA_IN[10]), .CARRY_IN(1'b0), .VAL_OUT(DATA_OUT[10]),
    .CARRY_OUT(n1bit_add_22_carry_out));
  _1BIT_ADD u_1bit_add_23 (
    .A_IN(n1bit_add_6_carry_out), .B_IN(DATA_IN[12]), .CARRY_IN(1'b0), .VAL_OUT(DATA_OUT[12]),
    .CARRY_OUT(n1bit_add_23_carry_out));
  _1BIT_ADD u_1bit_add_24 (
    .A_IN(n1bit_add_7_carry_out), .B_IN(DATA_IN[14]), .CARRY_IN(1'b0), .VAL_OUT(DATA_OUT[14]),
    .CARRY_OUT(n1bit_add_24_carry_out));
  _1BIT_ADD u_1bit_add_25 (
    .A_IN(n1bit_add_8_carry_out), .B_IN(DATA_IN[16]), .CARRY_IN(1'b0), .VAL_OUT(DATA_OUT[16]),
    .CARRY_OUT(n1bit_add_25_carry_out));
  _1BIT_ADD u_1bit_add_26 (
    .A_IN(n1bit_add_9_carry_out), .B_IN(DATA_IN[18]), .CARRY_IN(1'b0), .VAL_OUT(DATA_OUT[18]),
    .CARRY_OUT(n1bit_add_26_carry_out));
  _1BIT_ADD u_1bit_add_27 (
    .A_IN(n1bit_add_10_carry_out), .B_IN(DATA_IN[20]), .CARRY_IN(1'b0), .VAL_OUT(DATA_OUT[20]),
    .CARRY_OUT(n1bit_add_27_carry_out));
  _1BIT_ADD u_1bit_add_28 (
    .A_IN(n1bit_add_11_carry_out), .B_IN(DATA_IN[22]), .CARRY_IN(1'b0), .VAL_OUT(DATA_OUT[22]),
    .CARRY_OUT(n1bit_add_28_carry_out));
  _1BIT_ADD u_1bit_add_29 (
    .A_IN(n1bit_add_12_carry_out), .B_IN(DATA_IN[24]), .CARRY_IN(1'b0), .VAL_OUT(DATA_OUT[24]),
    .CARRY_OUT(n1bit_add_29_carry_out));
  _1BIT_ADD u_1bit_add_30 (
    .A_IN(n1bit_add_13_carry_out), .B_IN(DATA_IN[26]), .CARRY_IN(1'b0), .VAL_OUT(DATA_OUT[26]),
    .CARRY_OUT(n1bit_add_30_carry_out));
  _1BIT_ADD u_1bit_add_31 (
    .A_IN(n1bit_add_14_carry_out), .B_IN(DATA_IN[28]), .CARRY_IN(1'b0), .VAL_OUT(DATA_OUT[28]),
    .CARRY_OUT(n1bit_add_31_carry_out));
  _1BIT_ADD u_1bit_add_32 (
    .A_IN(n1bit_add_15_carry_out), .B_IN(DATA_IN[30]), .CARRY_IN(1'b0), .VAL_OUT(DATA_OUT[30]),
    .CARRY_OUT(n1bit_add_32_carry_out));
endmodule

module _24BITS_INC (
  input  [23:0] DATA_IN,
  output [23:0] DATA_OUT,
  output OVERFLOW_OUT
);

  wire [31:0] bit_extender_1_out, n32bits_inc_1_data_out;

  _32BITS_INC u_32bits_inc_1 (.DATA_IN(bit_extender_1_out), .DATA_OUT(n32bits_inc_1_data_out));  // open: OVERFLOW_OUT
  assign bit_extender_1_out = {{8{1'b0}}, DATA_IN};  // Bit_Extender bit_extender_1
  and and_1 (OVERFLOW_OUT, DATA_IN[0], DATA_IN[1], DATA_IN[2], DATA_IN[3], DATA_IN[4], DATA_IN[5], DATA_IN[6], DATA_IN[7], DATA_IN[8], DATA_IN[9], DATA_IN[10], DATA_IN[11], DATA_IN[12], DATA_IN[13], DATA_IN[14], DATA_IN[15], DATA_IN[16], DATA_IN[17], DATA_IN[18], DATA_IN[19], DATA_IN[20], DATA_IN[21], DATA_IN[22], DATA_IN[23], 1'b1);
  Bit_Extender #(.in_width(32), .out_width(24)) bit_extender_2 (.in(n32bits_inc_1_data_out), .out(DATA_OUT));
endmodule

// IF
module IF_STAGE (
  input  J_B_IN,
  input  [23:0] NEXT_PC_IN,
  input  FREEZE_IN,
  input  CLOCK_IN,
  input  RESET_IN,
  output INST_ADDR_OVERFLOW_OUT,
  output [23:0] PC_OUT,
  output [31:0] INSTRUCTION_OUT
);

  wire _24BITS_INC_overflow_out, not_1_out, not_2_out, or_1_out;
  wire [23:0] multiplexer_1_out, PC_q;

  Register #(.width(1)) ERR_SAVE (
    .D(_24BITS_INC_overflow_out), .Q(INST_ADDR_OVERFLOW_OUT), .clk(CLOCK_IN), .clr(RESET_IN));  // open: en
  or or_1 (or_1_out, INST_ADDR_OVERFLOW_OUT, RESET_IN);
  Multiplexer #(.width(24), .disabled(0), .enable("false")) multiplexer_1 (
    .in0(PC_OUT), .in1(NEXT_PC_IN), .out(multiplexer_1_out), .sel(J_B_IN));
  Register #(.width(24)) PC (.D(multiplexer_1_out), .en(not_1_out), .Q(PC_q), .clk(CLOCK_IN), .clr(or_1_out));
  not not_1 (not_1_out, FREEZE_IN);
  _24BITS_INC _24BITS_INC (.DATA_IN(PC_q), .DATA_OUT(PC_OUT), .OVERFLOW_OUT(_24BITS_INC_overflow_out));
  not not_2 (not_2_out, FREEZE_IN);
  RAM #(.addrWidth(24), .dataWidth(32)) ram_1 (
    .addr(PC_q), .data(INSTRUCTION_OUT), .sel(not_2_out), .clk(CLOCK_IN), .ld(not_2_out));  // open: clr

  // Notes on the sheet:
  //   INSTRUCTION MEM
endmodule

// REG
module MEM_BANK_DEC_EXE (
  input  [23:0] PC_IN,
  input  [5:0] OPC_IN,
  input  [5:0] FUNC_IN,
  input  [4:0] RS_IN,
  input  [4:0] RT_IN,
  input  [4:0] RD_IN,
  input  [4:0] SHIFT_IN,
  input  [15:0] IMM_IN,
  input  [31:0] VRS_IN,
  input  [31:0] VRT_IN,
  input  FREEZE_IN,
  input  CLOCK_IN,
  input  RESET_IN,
  output [23:0] PC_OUT,
  output [5:0] OPC_OUT,
  output [5:0] FUNC_OUT,
  output [4:0] RS_OUT,
  output [4:0] RT_OUT,
  output [4:0] RD_OUT,
  output [4:0] SHIFT_OUT,
  output [15:0] IMM_OUT,
  output [31:0] VRS_OUT,
  output [31:0] VRT_OUT
);

  wire not_1_out;

  Register #(.width(24)) register_1 (.D(PC_IN), .en(not_1_out), .Q(PC_OUT), .clk(CLOCK_IN), .clr(RESET_IN));
  Register #(.width(6)) register_2 (.D(OPC_IN), .en(not_1_out), .Q(OPC_OUT), .clk(CLOCK_IN), .clr(RESET_IN));
  Register #(.width(6)) register_3 (.D(FUNC_IN), .en(not_1_out), .Q(FUNC_OUT), .clk(CLOCK_IN), .clr(RESET_IN));
  Register #(.width(5)) register_4 (.D(RS_IN), .en(not_1_out), .Q(RS_OUT), .clk(CLOCK_IN), .clr(RESET_IN));
  Register #(.width(5)) register_5 (.D(RT_IN), .en(not_1_out), .Q(RT_OUT), .clk(CLOCK_IN), .clr(RESET_IN));
  Register #(.width(5)) register_6 (.D(RD_IN), .en(not_1_out), .Q(RD_OUT), .clk(CLOCK_IN), .clr(RESET_IN));
  Register #(.width(5)) register_7 (.D(SHIFT_IN), .en(not_1_out), .Q(SHIFT_OUT), .clk(CLOCK_IN), .clr(RESET_IN));
  Register #(.width(16)) register_8 (.D(IMM_IN), .en(not_1_out), .Q(IMM_OUT), .clk(CLOCK_IN), .clr(RESET_IN));
  Register #(.width(32)) register_9 (.D(VRS_IN), .en(not_1_out), .Q(VRS_OUT), .clk(CLOCK_IN), .clr(RESET_IN));
  Register #(.width(32)) register_10 (.D(VRT_IN), .en(not_1_out), .Q(VRT_OUT), .clk(CLOCK_IN), .clr(RESET_IN));
  not not_1 (not_1_out, FREEZE_IN);
endmodule

// DEC
module DEC_STAGE (
  input  [23:0] PC_IN,
  input  [31:0] INSTRUCTION_IN,
  input  [31:0] WRITE_DATA_IN,
  input  [4:0] REG_ADDR_IN,
  input  FREEZE_IN,
  input  CLOCK_IN,
  input  RESET_IN,
  output [23:0] PC_OUT,
  output [5:0] OPC_OUT,
  output [5:0] FUNC_OUT,
  output [4:0] RS_OUT,
  output [4:0] RT_OUT,
  output [4:0] RD_OUT,
  output [4:0] SHIFT_OUT,
  output [15:0] IMM_OUT,
  output [31:0] VRS_OUT,
  output [31:0] VRT_OUT
);

  REGISTER_FILE register_file_1 (
    .CLOCK_IN(CLOCK_IN), .RESET_IN(RESET_IN), .DATA_IN(WRITE_DATA_IN), .W_ADDR_IN(REG_ADDR_IN),
    .FREEZE_IN(FREEZE_IN), .ADDR_A_IN(INSTRUCTION_IN[25:21]), .ADDR_B_IN(INSTRUCTION_IN[20:16]),
    .DATA_OUT(VRS_OUT), .DATA_B_OUT(VRT_OUT));

  assign FUNC_OUT = INSTRUCTION_IN[5:0];
  assign IMM_OUT = INSTRUCTION_IN[15:0];
  assign OPC_OUT = INSTRUCTION_IN[31:26];
  assign PC_OUT = PC_IN;
  assign RD_OUT = INSTRUCTION_IN[15:11];
  assign RS_OUT = INSTRUCTION_IN[25:21];
  assign RT_OUT = INSTRUCTION_IN[20:16];
  assign SHIFT_OUT = INSTRUCTION_IN[10:6];

  // Notes on the sheet:
  //   RD
  //   SHIFT
  //   FUNC
  //   OPC
  //   RS
  //   RT
endmodule

module REGISTER_FILE (
  input  CLOCK_IN,
  input  RESET_IN,
  input  [31:0] DATA_IN,
  input  [4:0] W_ADDR_IN,
  input  FREEZE_IN,
  input  [4:0] ADDR_A_IN,
  input  [4:0] ADDR_B_IN,
  output [31:0] DATA_OUT,
  output [31:0] DATA_B_OUT
);

  wire decoder_1_out1, decoder_1_out2, decoder_1_out3, decoder_1_out4, decoder_1_out5, decoder_1_out6,
       decoder_1_out7, decoder_1_out8, decoder_1_out9, decoder_1_out10, decoder_1_out11, decoder_1_out12,
       decoder_1_out13, decoder_1_out14, decoder_1_out15, decoder_1_out16, decoder_1_out17, decoder_1_out18,
       decoder_1_out19, decoder_1_out20, decoder_1_out21, decoder_1_out22, decoder_1_out23, decoder_1_out24,
       decoder_1_out25, decoder_1_out26, decoder_1_out27, decoder_1_out28, decoder_1_out29, decoder_1_out30,
       decoder_1_out31, not_1_out;
  wire [31:0] register_1_q, register_2_q, register_3_q, register_4_q, register_5_q, register_6_q,
       register_7_q, register_8_q, register_9_q, register_10_q, register_11_q, register_12_q, register_13_q,
       register_14_q, register_15_q, register_16_q, register_17_q, register_18_q, register_19_q,
       register_20_q, register_21_q, register_22_q, register_23_q, register_24_q, register_25_q,
       register_26_q, register_27_q, register_28_q, register_29_q, register_30_q, register_31_q;

  not not_1 (not_1_out, FREEZE_IN);
  Decoder #(.select(5), .disabled(0)) decoder_1 (
    .out1(decoder_1_out1), .out2(decoder_1_out2), .out3(decoder_1_out3), .out4(decoder_1_out4),
    .out5(decoder_1_out5), .out6(decoder_1_out6), .out7(decoder_1_out7), .out8(decoder_1_out8),
    .out9(decoder_1_out9), .out10(decoder_1_out10), .out11(decoder_1_out11), .out12(decoder_1_out12),
    .out13(decoder_1_out13), .out14(decoder_1_out14), .out15(decoder_1_out15), .out16(decoder_1_out16),
    .out17(decoder_1_out17), .out18(decoder_1_out18), .out19(decoder_1_out19), .out20(decoder_1_out20),
    .out21(decoder_1_out21), .out22(decoder_1_out22), .out23(decoder_1_out23), .out24(decoder_1_out24),
    .out25(decoder_1_out25), .out26(decoder_1_out26), .out27(decoder_1_out27), .out28(decoder_1_out28),
    .out29(decoder_1_out29), .out30(decoder_1_out30), .out31(decoder_1_out31), .sel(W_ADDR_IN), .en(not_1_out));  // open: out0
  Register #(.width(32)) register_1 (
    .D(DATA_IN), .en(decoder_1_out17), .Q(register_1_q), .clk(CLOCK_IN), .clr(RESET_IN));
  Register #(.width(32)) register_2 (
    .D(DATA_IN), .en(decoder_1_out25), .Q(register_2_q), .clk(CLOCK_IN), .clr(RESET_IN));
  Register #(.width(32)) register_3 (
    .D(DATA_IN), .en(decoder_1_out1), .Q(register_3_q), .clk(CLOCK_IN), .clr(RESET_IN));
  Register #(.width(32)) register_4 (
    .D(DATA_IN), .en(decoder_1_out2), .Q(register_4_q), .clk(CLOCK_IN), .clr(RESET_IN));
  Register #(.width(32)) register_5 (
    .D(DATA_IN), .en(decoder_1_out10), .Q(register_5_q), .clk(CLOCK_IN), .clr(RESET_IN));
  Register #(.width(32)) register_6 (
    .D(DATA_IN), .en(decoder_1_out9), .Q(register_6_q), .clk(CLOCK_IN), .clr(RESET_IN));
  Register #(.width(32)) register_7 (
    .D(DATA_IN), .en(decoder_1_out18), .Q(register_7_q), .clk(CLOCK_IN), .clr(RESET_IN));
  Register #(.width(32)) register_8 (
    .D(DATA_IN), .en(decoder_1_out26), .Q(register_8_q), .clk(CLOCK_IN), .clr(RESET_IN));
  Register #(.width(32)) register_9 (
    .D(DATA_IN), .en(decoder_1_out3), .Q(register_9_q), .clk(CLOCK_IN), .clr(RESET_IN));
  Register #(.width(32)) register_10 (
    .D(DATA_IN), .en(decoder_1_out11), .Q(register_10_q), .clk(CLOCK_IN), .clr(RESET_IN));
  Register #(.width(32)) register_11 (
    .D(DATA_IN), .en(decoder_1_out19), .Q(register_11_q), .clk(CLOCK_IN), .clr(RESET_IN));
  Register #(.width(32)) register_12 (
    .D(DATA_IN), .en(decoder_1_out27), .Q(register_12_q), .clk(CLOCK_IN), .clr(RESET_IN));
  Register #(.width(32)) register_13 (
    .D(DATA_IN), .en(decoder_1_out4), .Q(register_13_q), .clk(CLOCK_IN), .clr(RESET_IN));
  Register #(.width(32)) register_14 (
    .D(DATA_IN), .en(decoder_1_out12), .Q(register_14_q), .clk(CLOCK_IN), .clr(RESET_IN));
  Register #(.width(32)) register_15 (
    .D(DATA_IN), .en(decoder_1_out21), .Q(register_15_q), .clk(CLOCK_IN), .clr(RESET_IN));
  Register #(.width(32)) register_16 (
    .D(DATA_IN), .en(decoder_1_out20), .Q(register_16_q), .clk(CLOCK_IN), .clr(RESET_IN));
  Register #(.width(32)) register_17 (
    .D(DATA_IN), .en(decoder_1_out29), .Q(register_17_q), .clk(CLOCK_IN), .clr(RESET_IN));
  Register #(.width(32)) register_18 (
    .D(DATA_IN), .en(decoder_1_out28), .Q(register_18_q), .clk(CLOCK_IN), .clr(RESET_IN));
  Register #(.width(32)) register_19 (
    .D(DATA_IN), .en(decoder_1_out5), .Q(register_19_q), .clk(CLOCK_IN), .clr(RESET_IN));
  Register #(.width(32)) register_20 (
    .D(DATA_IN), .en(decoder_1_out6), .Q(register_20_q), .clk(CLOCK_IN), .clr(RESET_IN));
  Register #(.width(32)) register_21 (
    .D(DATA_IN), .en(decoder_1_out13), .Q(register_21_q), .clk(CLOCK_IN), .clr(RESET_IN));
  Register #(.width(32)) register_22 (
    .D(DATA_IN), .en(decoder_1_out14), .Q(register_22_q), .clk(CLOCK_IN), .clr(RESET_IN));
  Register #(.width(32)) register_23 (
    .D(DATA_IN), .en(decoder_1_out22), .Q(register_23_q), .clk(CLOCK_IN), .clr(RESET_IN));
  Register #(.width(32)) register_24 (
    .D(DATA_IN), .en(decoder_1_out30), .Q(register_24_q), .clk(CLOCK_IN), .clr(RESET_IN));
  Register #(.width(32)) register_25 (
    .D(DATA_IN), .en(decoder_1_out7), .Q(register_25_q), .clk(CLOCK_IN), .clr(RESET_IN));
  Register #(.width(32)) register_26 (
    .D(DATA_IN), .en(decoder_1_out15), .Q(register_26_q), .clk(CLOCK_IN), .clr(RESET_IN));
  Register #(.width(32)) register_27 (
    .D(DATA_IN), .en(decoder_1_out23), .Q(register_27_q), .clk(CLOCK_IN), .clr(RESET_IN));
  Register #(.width(32)) register_28 (
    .D(DATA_IN), .en(decoder_1_out31), .Q(register_28_q), .clk(CLOCK_IN), .clr(RESET_IN));
  Register #(.width(32)) register_29 (
    .D(DATA_IN), .en(decoder_1_out8), .Q(register_29_q), .clk(CLOCK_IN), .clr(RESET_IN));
  Register #(.width(32)) register_30 (
    .D(DATA_IN), .en(decoder_1_out16), .Q(register_30_q), .clk(CLOCK_IN), .clr(RESET_IN));
  Register #(.width(32)) register_31 (
    .D(DATA_IN), .en(decoder_1_out24), .Q(register_31_q), .clk(CLOCK_IN), .clr(RESET_IN));
  Multiplexer #(.select(5), .width(32), .disabled(0)) multiplexer_1 (
    .in0({32{1'b0}}), .in1(register_3_q), .in2(register_4_q), .in3(register_9_q), .in4(register_13_q),
    .in5(register_19_q), .in6(register_20_q), .in7(register_25_q), .in8(register_29_q), .in9(register_6_q),
    .in10(register_5_q), .in11(register_10_q), .in12(register_14_q), .in13(register_21_q),
    .in14(register_22_q), .in15(register_26_q), .in16(register_30_q), .in17(register_1_q),
    .in18(register_7_q), .in19(register_11_q), .in20(register_16_q), .in21(register_15_q),
    .in22(register_23_q), .in23(register_27_q), .in24(register_31_q), .in25(register_2_q),
    .in26(register_8_q), .in27(register_12_q), .in28(register_18_q), .in29(register_17_q),
    .in30(register_24_q), .in31(register_28_q), .out(DATA_OUT), .sel(ADDR_A_IN), .en(not_1_out));
  Multiplexer #(.select(5), .width(32), .disabled(0)) multiplexer_2 (
    .in0({32{1'b0}}), .in1(register_3_q), .in2(register_4_q), .in3(register_9_q), .in4(register_13_q),
    .in5(register_19_q), .in6(register_20_q), .in7(register_25_q), .in8(register_29_q), .in9(register_6_q),
    .in10(register_5_q), .in11(register_10_q), .in12(register_14_q), .in13(register_21_q),
    .in14(register_22_q), .in15(register_26_q), .in16(register_30_q), .in17(register_1_q),
    .in18(register_7_q), .in19(register_11_q), .in20(register_16_q), .in21(register_15_q),
    .in22(register_23_q), .in23(register_27_q), .in24(register_31_q), .in25(register_2_q),
    .in26(register_8_q), .in27(register_12_q), .in28(register_18_q), .in29(register_17_q),
    .in30(register_24_q), .in31(register_28_q), .out(DATA_B_OUT), .sel(ADDR_B_IN), .en(not_1_out));

  // Notes on the sheet:
  //   R1-R8
  //   R9-R16
  //   R25-R31
  //   R17-R24
endmodule

// REG
module MEM_BANK_IF_DEC (
  input  [23:0] PC_IN,
  input  [31:0] INSTRUCTION_IN,
  input  FREEZE_IN,
  input  CLOCK_IN,
  input  RESET_IN,
  output [23:0] PC_OUT,
  output [31:0] INSTRUCTION_OUT
);

  wire not_1_out;

  not not_1 (not_1_out, FREEZE_IN);
  Register #(.width(24)) register_1 (.D(PC_IN), .en(not_1_out), .Q(PC_OUT), .clk(CLOCK_IN), .clr(RESET_IN));
  Register #(.width(32)) register_2 (
    .D(INSTRUCTION_IN), .en(not_1_out), .Q(INSTRUCTION_OUT), .clk(CLOCK_IN), .clr(RESET_IN));
endmodule

// EXE
module EXE_STAGE (
  input  [23:0] PC_IN,
  input  [5:0] OPC_IN,
  input  [5:0] FUNC_IN,
  input  [4:0] RS_IN,
  input  [4:0] RT_IN,
  input  [4:0] RD_IN,
  input  [4:0] SHIFT_IN,
  input  [15:0] IMM_IN,
  input  [31:0] VRS_IN,
  input  [31:0] VRT_IN,
  input  FREEZE_IN,
  input  CLOCK_IN,
  input  RESET_IN,
  output ALU_OVERFLOW_OUT,
  output J_B_OUT,
  output [23:0] PC_ADDR_OUT,
  output [23:0] PC_OUT,
  output [5:0] OPC_OUT,
  output [4:0] RS_OUT,
  output [4:0] RT_OUT,
  output [4:0] RD_OUT,
  output [31:0] ALU_OUT,
  output [31:0] VRT_OUT
);

  wire comparator_1_gt, n6bits_eq_comparator_1_eq_out;
  wire [31:0] bit_extender_1_out, multiplexer_2_out;

  _6BITS_EQ_COMPARATOR u_6bits_eq_comparator_1 (
    .A_IN(OPC_IN), .B_IN({6{1'b0}}), .EQ_OUT(n6bits_eq_comparator_1_eq_out));
  Multiplexer #(.width(6), .enable("false")) multiplexer_1 (
    .in1(FUNC_IN), .out(OPC_OUT), .sel(n6bits_eq_comparator_1_eq_out));  // open: in0
  assign bit_extender_1_out = {{27{1'b0}}, SHIFT_IN};  // Bit_Extender bit_extender_1
  Comparator #(.width(6), .mode("unsigned")) comparator_1 (
    .a(OPC_OUT), .b(6'b001000), .gt(comparator_1_gt));  // open: eq, lt
  Multiplexer #(.width(32), .disabled(0), .enable("false")) multiplexer_2 (
    .in0(bit_extender_1_out), .in1(VRT_IN), .out(multiplexer_2_out), .sel(comparator_1_gt));
  ALU alu_1 (
    .OP_1_IN(VRS_IN), .OP_2_IN(multiplexer_2_out), .FUNCTION_IN(OPC_OUT), .ALU_OUT(ALU_OUT),
    .OVERFLOW(ALU_OVERFLOW_OUT), .J_B_OUT(J_B_OUT), .CLOCK_IN(CLOCK_IN), .RESET_IN(RESET_IN));
  Bit_Extender #(.in_width(32), .out_width(24)) bit_extender_2 (.in(ALU_OUT), .out(PC_ADDR_OUT));

  assign PC_OUT = PC_IN;
  assign RD_OUT = RD_IN;
  assign RS_OUT = RS_IN;
  assign RT_OUT = RT_IN;
  assign VRT_OUT = VRT_IN;

  // Notes on the sheet:
  //   ACTUAL OPC
  //   TEST RT/SHIFT
endmodule

// NEQ_COMP
module _6BITS_NEQ_COMPARATOR (
  input  [5:0] A_IN,
  input  [5:0] B_IN,
  output EQ_OUT
);

  wire xor_1_out, xor_2_out, xor_3_out, xor_4_out, xor_5_out, xor_6_out;

  xor xor_1 (xor_1_out, A_IN[0], B_IN[0]);
  xor xor_2 (xor_2_out, A_IN[1], B_IN[1]);
  xor xor_3 (xor_3_out, A_IN[2], B_IN[2]);
  xor xor_4 (xor_4_out, A_IN[3], B_IN[3]);
  xor xor_5 (xor_5_out, A_IN[4], B_IN[4]);
  xor xor_6 (xor_6_out, A_IN[5], B_IN[5]);
  or or_1 (EQ_OUT, xor_1_out, xor_2_out, xor_3_out, xor_4_out, xor_5_out, xor_6_out);
endmodule

module ALU (
  input  [31:0] OP_1_IN,
  input  [31:0] OP_2_IN,
  input  [5:0] FUNCTION_IN,
  input  CLOCK_IN,
  input  RESET_IN,
  output OVERFLOW,
  output [31:0] ALU_OUT,
  output J_B_OUT
);

  wire adder_1_cout, ALU_FUNC_CTRL_hi_lo_en_out, comparator_1_lt, comparator_2_lt, subtractor_1_bout;
  wire [5:0] ALU_FUNC_CTRL_selector_out;
  wire [31:0] adder_1_out, bit_extender_1_out, bit_extender_2_out, divider_1_out, divider_1_rem, HI_q, LO_q,
       multiplexer_1_out, multiplexer_2_out, multiplier_1_cout, multiplier_1_out, n32bits_and_1_and_out,
       n32bits_nor_1_nor_out, n32bits_or_1_or_out, n32bits_xor_1_xor_out, or_2_out, or_3_out, shifter_1_out,
       shifter_2_out, shifter_3_out, subtractor_1_out;

  ALU_FUNC_SELECTOR ALU_FUNC_CTRL (
    .FUNC_VAL_IN(FUNCTION_IN), .SELECTOR_OUT(ALU_FUNC_CTRL_selector_out),
    .HI_LO_EN_OUT(ALU_FUNC_CTRL_hi_lo_en_out), .J_B_OUT(J_B_OUT));
  Adder #(.width(32)) adder_1 (.a(OP_1_IN), .b(OP_2_IN), .out(adder_1_out), .cout(adder_1_cout));  // open: cin
  _32BITS_AND u_32bits_and_1 (.DATA_0_IN(OP_1_IN), .DATA_1_IN(OP_2_IN), .AND_OUT(n32bits_and_1_and_out));
  Divider #(.width(32)) divider_1 (.a(OP_1_IN), .b(OP_2_IN), .out(divider_1_out), .rem(divider_1_rem));  // open: upper
  Multiplier #(.width(32)) multiplier_1 (
    .a(OP_1_IN), .b(OP_2_IN), .out(multiplier_1_out), .cout(multiplier_1_cout));  // open: cin
  _32BITS_NOR u_32bits_nor_1 (.DATA_0_IN(OP_1_IN), .DATA_1_IN(OP_2_IN), .NOR_OUT(n32bits_nor_1_nor_out));
  _32BITS_XOR u_32bits_xor_1 (.DATA_0_IN(OP_1_IN), .DATA_1_IN(OP_2_IN), .XOR_OUT(n32bits_xor_1_xor_out));
  _32BITS_OR u_32bits_or_1 (.DATA_0_IN(OP_1_IN), .DATA_1_IN(OP_2_IN), .OR_OUT(n32bits_or_1_or_out));
  Comparator #(.width(32)) comparator_1 (.a(OP_1_IN), .b(OP_2_IN), .lt(comparator_1_lt));  // open: gt, eq
  assign bit_extender_1_out = {{31{1'b0}}, comparator_1_lt};  // Bit_Extender bit_extender_1
  Comparator #(.width(32), .mode("unsigned")) comparator_2 (
    .a(OP_1_IN), .b(OP_2_IN), .lt(comparator_2_lt));  // open: gt, eq
  assign bit_extender_2_out = {{31{1'b0}}, comparator_2_lt};  // Bit_Extender bit_extender_2
  Shifter #(.width(32)) shifter_1 (.in(OP_1_IN), .\dist (OP_2_IN[4:0]), .out(shifter_1_out));
  Shifter #(.width(32), .shift("lr")) shifter_2 (.in(OP_1_IN), .\dist (OP_2_IN[4:0]), .out(shifter_2_out));
  Shifter #(.width(32), .shift("ar")) shifter_3 (.in(OP_1_IN), .\dist (OP_2_IN[4:0]), .out(shifter_3_out));
  Subtractor #(.width(32)) subtractor_1 (
    .a(OP_1_IN), .b(OP_1_IN), .out(subtractor_1_out), .bout(subtractor_1_bout));  // open: bin
  or or_1 (OVERFLOW, adder_1_cout, subtractor_1_bout);
  assign or_2_out = divider_1_rem | multiplier_1_cout;  // OR_Gate or_2, 32 bits wide
  assign or_3_out = divider_1_out | multiplier_1_out;  // OR_Gate or_3, 32 bits wide
  Register #(.width(32)) HI (.D(or_2_out), .Q(HI_q), .clk(CLOCK_IN), .clr(RESET_IN));  // open: en
  Register #(.width(32)) LO (.D(or_3_out), .en(ALU_FUNC_CTRL_hi_lo_en_out), .Q(LO_q), .clk(CLOCK_IN), .clr(RESET_IN));
  Multiplexer #(.select(5), .width(32), .disabled(0), .enable("false")) multiplexer_1 (
    .in1(adder_1_out), .in2(adder_1_out), .in3(n32bits_and_1_and_out), .in6(OP_1_IN), .in7(HI_q), .in8(LO_q),
    .in11(n32bits_nor_1_nor_out), .in12(n32bits_xor_1_xor_out), .in13(n32bits_or_1_or_out),
    .in14(bit_extender_1_out), .in15(bit_extender_2_out), .in16(shifter_1_out), .in17(shifter_2_out),
    .in18(shifter_3_out), .in19(subtractor_1_out), .in20(subtractor_1_out), .out(multiplexer_1_out),
    .sel(ALU_FUNC_CTRL_selector_out[4:0]));  // open: in0, in4, in5, in9, in10, in21, in22, in23, in24, in25, in26, in27, in28, in29, in30, in31
  Multiplexer #(.select(5), .width(32), .disabled(0), .enable("false")) multiplexer_2 (
    .out(multiplexer_2_out), .sel(ALU_FUNC_CTRL_selector_out[4:0]));  // open: in0, in1, in2, in3, in4, in5, in6, in7, in8, in9, in10, in11, in12, in13, in14, in15, in16, in17, in18, in19, in20, in21, in22, in23, in24, in25, in26, in27, in28, in29, in30, in31
  Multiplexer #(.width(32), .disabled(0), .enable("false")) multiplexer_3 (
    .in0(multiplexer_1_out), .in1(multiplexer_2_out), .out(ALU_OUT), .sel(ALU_FUNC_CTRL_selector_out[5]));

  // Notes on the sheet:
  //   JR
  //   MULT/MULTU
  //   STL
  //   STLU
  //   SLL
  //   SRL
  //   SRA
  //   SUB/SUBU
  //   MFHI
  //   MFLO
endmodule

// EQ
module _6BITS_EQ_COMPARATOR (
  input  [5:0] A_IN,
  input  [5:0] B_IN,
  output EQ_OUT
);

  wire xor_1_out, xor_2_out, xor_3_out, xor_4_out, xor_5_out, xor_6_out;

  xor xor_1 (xor_1_out, A_IN[0], B_IN[0]);
  xor xor_2 (xor_2_out, A_IN[1], B_IN[1]);
  xor xor_3 (xor_3_out, A_IN[2], B_IN[2]);
  xor xor_4 (xor_4_out, A_IN[3], B_IN[3]);
  xor xor_5 (xor_5_out, A_IN[4], B_IN[4]);
  xor xor_6 (xor_6_out, A_IN[5], B_IN[5]);
  nor nor_1 (EQ_OUT, xor_1_out, xor_2_out, xor_3_out, xor_4_out, xor_5_out, xor_6_out);
endmodule

module ALU_FUNC_SELECTOR (
  input  [5:0] FUNC_VAL_IN,
  output [5:0] SELECTOR_OUT,
  output HI_LO_EN_OUT,
  output J_B_OUT
);

  wire AND_eq_out, DIV_eq_out, DIVU_eq_out, JR_eq_out, MFLO_eq_out, MULT_eq_out, MULTU_eq_out,
       n6bits_eq_comparator_1_eq_out, n6bits_eq_comparator_2_eq_out, NOR_eq_out, OR_eq_out, SLL_eq_out,
       SLT_eq_out, SLTU_eq_out, SRA_eq_out, SRL_eq_out, SUB_eq_out, SUBU_eq_out, XOR_eq_out;

  _6BITS_EQ_COMPARATOR u_6bits_eq_comparator_1 (
    .A_IN(FUNC_VAL_IN), .B_IN(6'b100000), .EQ_OUT(n6bits_eq_comparator_1_eq_out));
  _6BITS_EQ_COMPARATOR u_6bits_eq_comparator_2 (
    .A_IN(FUNC_VAL_IN), .B_IN(6'b100001), .EQ_OUT(n6bits_eq_comparator_2_eq_out));
  _6BITS_EQ_COMPARATOR AND (.A_IN(FUNC_VAL_IN), .B_IN(6'b100100), .EQ_OUT(AND_eq_out));
  _6BITS_EQ_COMPARATOR DIV (.A_IN(FUNC_VAL_IN), .B_IN(6'b011010), .EQ_OUT(DIV_eq_out));
  _6BITS_EQ_COMPARATOR DIVU (.A_IN(FUNC_VAL_IN), .B_IN(6'b011011), .EQ_OUT(DIVU_eq_out));
  _6BITS_EQ_COMPARATOR JR (.A_IN(FUNC_VAL_IN), .B_IN(6'b001000), .EQ_OUT(JR_eq_out));
  _6BITS_EQ_COMPARATOR MFHI (.A_IN(FUNC_VAL_IN), .B_IN(6'b010000), .EQ_OUT(J_B_OUT));
  _6BITS_EQ_COMPARATOR MFLO (.A_IN(FUNC_VAL_IN), .B_IN(6'b010010), .EQ_OUT(MFLO_eq_out));
  _6BITS_EQ_COMPARATOR MULT (.A_IN(FUNC_VAL_IN), .B_IN(6'b011000), .EQ_OUT(MULT_eq_out));
  _6BITS_EQ_COMPARATOR MULTU (.A_IN(FUNC_VAL_IN), .B_IN(6'b011001), .EQ_OUT(MULTU_eq_out));
  _6BITS_EQ_COMPARATOR NOR (.A_IN(FUNC_VAL_IN), .B_IN(6'b100111), .EQ_OUT(NOR_eq_out));
  _6BITS_EQ_COMPARATOR XOR (.A_IN(FUNC_VAL_IN), .B_IN(6'b100110), .EQ_OUT(XOR_eq_out));
  _6BITS_EQ_COMPARATOR OR (.A_IN(FUNC_VAL_IN), .B_IN(6'b100101), .EQ_OUT(OR_eq_out));
  _6BITS_EQ_COMPARATOR SLT (.A_IN(FUNC_VAL_IN), .B_IN(6'b101010), .EQ_OUT(SLT_eq_out));
  _6BITS_EQ_COMPARATOR SLTU (.A_IN(FUNC_VAL_IN), .B_IN(6'b101011), .EQ_OUT(SLTU_eq_out));
  _6BITS_EQ_COMPARATOR SLL (.A_IN(FUNC_VAL_IN), .B_IN({6{1'b0}}), .EQ_OUT(SLL_eq_out));
  _6BITS_EQ_COMPARATOR SRL (.A_IN(FUNC_VAL_IN), .B_IN(6'b000010), .EQ_OUT(SRL_eq_out));
  _6BITS_EQ_COMPARATOR SRA (.A_IN(FUNC_VAL_IN), .B_IN(6'b000011), .EQ_OUT(SRA_eq_out));
  _6BITS_EQ_COMPARATOR SUB (.A_IN(FUNC_VAL_IN), .B_IN(6'b100010), .EQ_OUT(SUB_eq_out));
  _6BITS_EQ_COMPARATOR SUBU (.A_IN(FUNC_VAL_IN), .B_IN(6'b100011), .EQ_OUT(SUBU_eq_out));
  buf or_2 (SELECTOR_OUT[5], 1'b0);  // OR_Gate
  or or_3 (HI_LO_EN_OUT, DIV_eq_out, DIVU_eq_out, MULT_eq_out, MULTU_eq_out);
  or or_4 (SELECTOR_OUT[4], SUBU_eq_out, SUB_eq_out, SRA_eq_out, SRL_eq_out, SLL_eq_out);
  or or_5 (SELECTOR_OUT[3], SLTU_eq_out, SLT_eq_out, OR_eq_out, XOR_eq_out, MFLO_eq_out, NOR_eq_out, MULTU_eq_out, MULT_eq_out);
  or or_6 (SELECTOR_OUT[0], n6bits_eq_comparator_1_eq_out, AND_eq_out, DIVU_eq_out, MULT_eq_out, NOR_eq_out, J_B_OUT, OR_eq_out, SLTU_eq_out, SRL_eq_out, SUB_eq_out);
  or or_7 (SELECTOR_OUT[1], n6bits_eq_comparator_2_eq_out, AND_eq_out, MULTU_eq_out, NOR_eq_out, J_B_OUT, JR_eq_out, SLT_eq_out, SLTU_eq_out, SRA_eq_out, SUB_eq_out);
  or or_8 (SELECTOR_OUT[2], DIV_eq_out, DIVU_eq_out, JR_eq_out, J_B_OUT, XOR_eq_out, OR_eq_out, SLT_eq_out, SLTU_eq_out, SUBU_eq_out);

  // Notes on the sheet:
  //   ADD
  //   ADDU
endmodule

module _32BITS_ADD_U (
  input  [31:0] DATA_0_IN,
  input  [31:0] DATA_1_IN,
  output [31:0] DATA_OUT,
  output OVERFLOW_OUT
);

  wire n1bit_add_1_carry_out, n1bit_add_2_carry_out, n1bit_add_3_carry_out, n1bit_add_4_carry_out,
       n1bit_add_5_carry_out, n1bit_add_6_carry_out, n1bit_add_7_carry_out, n1bit_add_8_carry_out,
       n1bit_add_9_carry_out, n1bit_add_10_carry_out, n1bit_add_11_carry_out, n1bit_add_12_carry_out,
       n1bit_add_13_carry_out, n1bit_add_14_carry_out, n1bit_add_15_carry_out, n1bit_add_16_carry_out,
       n1bit_add_17_carry_out, n1bit_add_18_carry_out, n1bit_add_19_carry_out, n1bit_add_20_carry_out,
       n1bit_add_21_carry_out, n1bit_add_22_carry_out, n1bit_add_23_carry_out, n1bit_add_24_carry_out,
       n1bit_add_25_carry_out, n1bit_add_26_carry_out, n1bit_add_27_carry_out, n1bit_add_28_carry_out,
       n1bit_add_29_carry_out, n1bit_add_30_carry_out, n1bit_add_31_carry_out;

  _1BIT_ADD u_1bit_add_1 (
    .A_IN(DATA_0_IN[0]), .B_IN(DATA_1_IN[0]), .CARRY_IN(1'b0), .VAL_OUT(DATA_OUT[0]),
    .CARRY_OUT(n1bit_add_1_carry_out));
  _1BIT_ADD u_1bit_add_2 (
    .A_IN(DATA_0_IN[1]), .B_IN(DATA_1_IN[1]), .CARRY_IN(n1bit_add_1_carry_out), .VAL_OUT(DATA_OUT[1]),
    .CARRY_OUT(n1bit_add_2_carry_out));
  _1BIT_ADD u_1bit_add_3 (
    .A_IN(DATA_0_IN[2]), .B_IN(DATA_1_IN[2]), .CARRY_IN(n1bit_add_2_carry_out), .VAL_OUT(DATA_OUT[2]),
    .CARRY_OUT(n1bit_add_3_carry_out));
  _1BIT_ADD u_1bit_add_4 (
    .A_IN(DATA_0_IN[3]), .B_IN(DATA_1_IN[3]), .CARRY_IN(n1bit_add_3_carry_out), .VAL_OUT(DATA_OUT[3]),
    .CARRY_OUT(n1bit_add_4_carry_out));
  _1BIT_ADD u_1bit_add_5 (
    .A_IN(DATA_0_IN[4]), .B_IN(DATA_1_IN[4]), .CARRY_IN(n1bit_add_4_carry_out), .VAL_OUT(DATA_OUT[4]),
    .CARRY_OUT(n1bit_add_5_carry_out));
  _1BIT_ADD u_1bit_add_6 (
    .A_IN(DATA_0_IN[5]), .B_IN(DATA_1_IN[5]), .CARRY_IN(n1bit_add_5_carry_out), .VAL_OUT(DATA_OUT[5]),
    .CARRY_OUT(n1bit_add_6_carry_out));
  _1BIT_ADD u_1bit_add_7 (
    .A_IN(DATA_0_IN[6]), .B_IN(DATA_1_IN[6]), .CARRY_IN(n1bit_add_6_carry_out), .VAL_OUT(DATA_OUT[6]),
    .CARRY_OUT(n1bit_add_7_carry_out));
  _1BIT_ADD u_1bit_add_8 (
    .A_IN(DATA_0_IN[7]), .B_IN(DATA_1_IN[7]), .CARRY_IN(n1bit_add_7_carry_out), .VAL_OUT(DATA_OUT[7]),
    .CARRY_OUT(n1bit_add_8_carry_out));
  _1BIT_ADD u_1bit_add_9 (
    .A_IN(DATA_0_IN[8]), .B_IN(DATA_1_IN[8]), .CARRY_IN(n1bit_add_8_carry_out), .VAL_OUT(DATA_OUT[8]),
    .CARRY_OUT(n1bit_add_9_carry_out));
  _1BIT_ADD u_1bit_add_10 (
    .A_IN(DATA_0_IN[9]), .B_IN(DATA_1_IN[9]), .CARRY_IN(n1bit_add_9_carry_out), .VAL_OUT(DATA_OUT[9]),
    .CARRY_OUT(n1bit_add_10_carry_out));
  _1BIT_ADD u_1bit_add_11 (
    .A_IN(DATA_0_IN[10]), .B_IN(DATA_1_IN[10]), .CARRY_IN(n1bit_add_10_carry_out), .VAL_OUT(DATA_OUT[10]),
    .CARRY_OUT(n1bit_add_11_carry_out));
  _1BIT_ADD u_1bit_add_12 (
    .A_IN(DATA_0_IN[11]), .B_IN(DATA_1_IN[11]), .CARRY_IN(n1bit_add_11_carry_out), .VAL_OUT(DATA_OUT[11]),
    .CARRY_OUT(n1bit_add_12_carry_out));
  _1BIT_ADD u_1bit_add_13 (
    .A_IN(DATA_0_IN[12]), .B_IN(DATA_1_IN[12]), .CARRY_IN(n1bit_add_12_carry_out), .VAL_OUT(DATA_OUT[12]),
    .CARRY_OUT(n1bit_add_13_carry_out));
  _1BIT_ADD u_1bit_add_14 (
    .A_IN(DATA_0_IN[13]), .B_IN(DATA_1_IN[13]), .CARRY_IN(n1bit_add_13_carry_out), .VAL_OUT(DATA_OUT[13]),
    .CARRY_OUT(n1bit_add_14_carry_out));
  _1BIT_ADD u_1bit_add_15 (
    .A_IN(DATA_0_IN[14]), .B_IN(DATA_1_IN[14]), .CARRY_IN(n1bit_add_14_carry_out), .VAL_OUT(DATA_OUT[14]),
    .CARRY_OUT(n1bit_add_15_carry_out));
  _1BIT_ADD u_1bit_add_16 (
    .A_IN(DATA_0_IN[15]), .B_IN(DATA_1_IN[15]), .CARRY_IN(n1bit_add_15_carry_out), .VAL_OUT(DATA_OUT[15]),
    .CARRY_OUT(n1bit_add_16_carry_out));
  _1BIT_ADD u_1bit_add_17 (
    .A_IN(DATA_0_IN[16]), .B_IN(DATA_1_IN[16]), .CARRY_IN(n1bit_add_16_carry_out), .VAL_OUT(DATA_OUT[16]),
    .CARRY_OUT(n1bit_add_17_carry_out));
  _1BIT_ADD u_1bit_add_18 (
    .A_IN(DATA_0_IN[17]), .B_IN(DATA_1_IN[17]), .CARRY_IN(n1bit_add_17_carry_out), .VAL_OUT(DATA_OUT[17]),
    .CARRY_OUT(n1bit_add_18_carry_out));
  _1BIT_ADD u_1bit_add_19 (
    .A_IN(DATA_0_IN[18]), .B_IN(DATA_1_IN[18]), .CARRY_IN(n1bit_add_18_carry_out), .VAL_OUT(DATA_OUT[18]),
    .CARRY_OUT(n1bit_add_19_carry_out));
  _1BIT_ADD u_1bit_add_20 (
    .A_IN(DATA_0_IN[19]), .B_IN(DATA_1_IN[19]), .CARRY_IN(n1bit_add_19_carry_out), .VAL_OUT(DATA_OUT[19]),
    .CARRY_OUT(n1bit_add_20_carry_out));
  _1BIT_ADD u_1bit_add_21 (
    .A_IN(DATA_0_IN[20]), .B_IN(DATA_1_IN[20]), .CARRY_IN(n1bit_add_20_carry_out), .VAL_OUT(DATA_OUT[20]),
    .CARRY_OUT(n1bit_add_21_carry_out));
  _1BIT_ADD u_1bit_add_22 (
    .A_IN(DATA_0_IN[21]), .B_IN(DATA_1_IN[21]), .CARRY_IN(n1bit_add_21_carry_out), .VAL_OUT(DATA_OUT[21]),
    .CARRY_OUT(n1bit_add_22_carry_out));
  _1BIT_ADD u_1bit_add_23 (
    .A_IN(DATA_0_IN[22]), .B_IN(DATA_1_IN[22]), .CARRY_IN(n1bit_add_22_carry_out), .VAL_OUT(DATA_OUT[22]),
    .CARRY_OUT(n1bit_add_23_carry_out));
  _1BIT_ADD u_1bit_add_24 (
    .A_IN(DATA_0_IN[23]), .B_IN(DATA_1_IN[23]), .CARRY_IN(n1bit_add_23_carry_out), .VAL_OUT(DATA_OUT[23]),
    .CARRY_OUT(n1bit_add_24_carry_out));
  _1BIT_ADD u_1bit_add_25 (
    .A_IN(DATA_0_IN[24]), .B_IN(DATA_1_IN[24]), .CARRY_IN(n1bit_add_24_carry_out), .VAL_OUT(DATA_OUT[24]),
    .CARRY_OUT(n1bit_add_25_carry_out));
  _1BIT_ADD u_1bit_add_26 (
    .A_IN(DATA_0_IN[25]), .B_IN(DATA_1_IN[25]), .CARRY_IN(n1bit_add_25_carry_out), .VAL_OUT(DATA_OUT[25]),
    .CARRY_OUT(n1bit_add_26_carry_out));
  _1BIT_ADD u_1bit_add_27 (
    .A_IN(DATA_0_IN[26]), .B_IN(DATA_1_IN[26]), .CARRY_IN(n1bit_add_26_carry_out), .VAL_OUT(DATA_OUT[26]),
    .CARRY_OUT(n1bit_add_27_carry_out));
  _1BIT_ADD u_1bit_add_28 (
    .A_IN(DATA_0_IN[27]), .B_IN(DATA_1_IN[27]), .CARRY_IN(n1bit_add_27_carry_out), .VAL_OUT(DATA_OUT[27]),
    .CARRY_OUT(n1bit_add_28_carry_out));
  _1BIT_ADD u_1bit_add_29 (
    .A_IN(DATA_0_IN[28]), .B_IN(DATA_1_IN[28]), .CARRY_IN(n1bit_add_28_carry_out), .VAL_OUT(DATA_OUT[28]),
    .CARRY_OUT(n1bit_add_29_carry_out));
  _1BIT_ADD u_1bit_add_30 (
    .A_IN(DATA_0_IN[29]), .B_IN(DATA_1_IN[29]), .CARRY_IN(n1bit_add_29_carry_out), .VAL_OUT(DATA_OUT[29]),
    .CARRY_OUT(n1bit_add_30_carry_out));
  _1BIT_ADD u_1bit_add_31 (
    .A_IN(DATA_0_IN[30]), .B_IN(DATA_1_IN[30]), .CARRY_IN(n1bit_add_30_carry_out), .VAL_OUT(DATA_OUT[30]),
    .CARRY_OUT(n1bit_add_31_carry_out));
  _1BIT_ADD u_1bit_add_32 (
    .A_IN(DATA_0_IN[31]), .B_IN(DATA_1_IN[31]), .CARRY_IN(n1bit_add_31_carry_out), .VAL_OUT(DATA_OUT[31]),
    .CARRY_OUT(OVERFLOW_OUT));
endmodule

// AND
module _32BITS_AND (
  input  [31:0] DATA_0_IN,
  input  [31:0] DATA_1_IN,
  output [31:0] AND_OUT
);

  and and_1 (AND_OUT[0], DATA_0_IN[0], DATA_1_IN[0]);
  and and_2 (AND_OUT[1], DATA_0_IN[1], DATA_1_IN[1]);
  and and_3 (AND_OUT[2], DATA_0_IN[2], DATA_1_IN[2]);
  and and_4 (AND_OUT[3], DATA_0_IN[3], DATA_1_IN[3]);
  and and_5 (AND_OUT[4], DATA_0_IN[4], DATA_1_IN[4]);
  and and_6 (AND_OUT[5], DATA_0_IN[5], DATA_1_IN[5]);
  and and_7 (AND_OUT[6], DATA_0_IN[6], DATA_1_IN[6]);
  and and_8 (AND_OUT[7], DATA_0_IN[7], DATA_1_IN[7]);
  and and_9 (AND_OUT[8], DATA_0_IN[8], DATA_1_IN[8]);
  and and_10 (AND_OUT[9], DATA_0_IN[9], DATA_1_IN[9]);
  and and_11 (AND_OUT[10], DATA_0_IN[10], DATA_1_IN[10]);
  and and_12 (AND_OUT[11], DATA_0_IN[11], DATA_1_IN[11]);
  and and_13 (AND_OUT[12], DATA_0_IN[12], DATA_1_IN[12]);
  and and_14 (AND_OUT[13], DATA_0_IN[13], DATA_1_IN[13]);
  and and_15 (AND_OUT[14], DATA_0_IN[14], DATA_1_IN[14]);
  and and_16 (AND_OUT[15], DATA_0_IN[15], DATA_1_IN[15]);
  and and_17 (AND_OUT[16], DATA_0_IN[16], DATA_1_IN[16]);
  and and_18 (AND_OUT[17], DATA_0_IN[17], DATA_1_IN[17]);
  and and_19 (AND_OUT[18], DATA_0_IN[18], DATA_1_IN[18]);
  and and_20 (AND_OUT[19], DATA_0_IN[19], DATA_1_IN[19]);
  and and_21 (AND_OUT[20], DATA_0_IN[20], DATA_1_IN[20]);
  and and_22 (AND_OUT[21], DATA_0_IN[21], DATA_1_IN[21]);
  and and_23 (AND_OUT[22], DATA_0_IN[22], DATA_1_IN[22]);
  and and_24 (AND_OUT[23], DATA_0_IN[23], DATA_1_IN[23]);
  and and_25 (AND_OUT[24], DATA_0_IN[24], DATA_1_IN[24]);
  and and_26 (AND_OUT[25], DATA_0_IN[25], DATA_1_IN[25]);
  and and_27 (AND_OUT[26], DATA_0_IN[26], DATA_1_IN[26]);
  and and_28 (AND_OUT[27], DATA_0_IN[27], DATA_1_IN[27]);
  and and_29 (AND_OUT[28], DATA_0_IN[28], DATA_1_IN[28]);
  and and_30 (AND_OUT[29], DATA_0_IN[29], DATA_1_IN[29]);
  and and_31 (AND_OUT[30], DATA_0_IN[30], DATA_1_IN[30]);
  and and_32 (AND_OUT[31], DATA_0_IN[31], DATA_1_IN[31]);
endmodule

// NOR
module _32BITS_NOR (
  input  [31:0] DATA_0_IN,
  input  [31:0] DATA_1_IN,
  output [31:0] NOR_OUT
);

  nor nor_1 (NOR_OUT[0], DATA_0_IN[0], DATA_1_IN[0]);
  nor nor_2 (NOR_OUT[1], DATA_0_IN[1], DATA_1_IN[1]);
  nor nor_3 (NOR_OUT[2], DATA_0_IN[2], DATA_1_IN[2]);
  nor nor_4 (NOR_OUT[3], DATA_0_IN[3], DATA_1_IN[3]);
  nor nor_5 (NOR_OUT[4], DATA_0_IN[4], DATA_1_IN[4]);
  nor nor_6 (NOR_OUT[5], DATA_0_IN[5], DATA_1_IN[5]);
  nor nor_7 (NOR_OUT[6], DATA_0_IN[6], DATA_1_IN[6]);
  nor nor_8 (NOR_OUT[7], DATA_0_IN[7], DATA_1_IN[7]);
  nor nor_9 (NOR_OUT[8], DATA_0_IN[8], DATA_1_IN[8]);
  nor nor_10 (NOR_OUT[9], DATA_0_IN[9], DATA_1_IN[9]);
  nor nor_11 (NOR_OUT[10], DATA_0_IN[10], DATA_1_IN[10]);
  nor nor_12 (NOR_OUT[11], DATA_0_IN[11], DATA_1_IN[11]);
  nor nor_13 (NOR_OUT[12], DATA_0_IN[12], DATA_1_IN[12]);
  nor nor_14 (NOR_OUT[13], DATA_0_IN[13], DATA_1_IN[13]);
  nor nor_15 (NOR_OUT[14], DATA_0_IN[14], DATA_1_IN[14]);
  nor nor_16 (NOR_OUT[15], DATA_0_IN[15], DATA_1_IN[15]);
  nor nor_17 (NOR_OUT[16], DATA_0_IN[16], DATA_1_IN[16]);
  nor nor_18 (NOR_OUT[17], DATA_0_IN[17], DATA_1_IN[17]);
  nor nor_19 (NOR_OUT[18], DATA_0_IN[18], DATA_1_IN[18]);
  nor nor_20 (NOR_OUT[19], DATA_0_IN[19], DATA_1_IN[19]);
  nor nor_21 (NOR_OUT[20], DATA_0_IN[20], DATA_1_IN[20]);
  nor nor_22 (NOR_OUT[21], DATA_0_IN[21], DATA_1_IN[21]);
  nor nor_23 (NOR_OUT[22], DATA_0_IN[22], DATA_1_IN[22]);
  nor nor_24 (NOR_OUT[23], DATA_0_IN[23], DATA_1_IN[23]);
  nor nor_25 (NOR_OUT[24], DATA_0_IN[24], DATA_1_IN[24]);
  nor nor_26 (NOR_OUT[25], DATA_0_IN[25], DATA_1_IN[25]);
  nor nor_27 (NOR_OUT[26], DATA_0_IN[26], DATA_1_IN[26]);
  nor nor_28 (NOR_OUT[27], DATA_0_IN[27], DATA_1_IN[27]);
  nor nor_29 (NOR_OUT[28], DATA_0_IN[28], DATA_1_IN[28]);
  nor nor_30 (NOR_OUT[29], DATA_0_IN[29], DATA_1_IN[29]);
  nor nor_31 (NOR_OUT[30], DATA_0_IN[30], DATA_1_IN[30]);
  nor nor_32 (NOR_OUT[31], DATA_0_IN[31], DATA_1_IN[31]);
endmodule

// XOR
module _32BITS_XOR (
  input  [31:0] DATA_0_IN,
  input  [31:0] DATA_1_IN,
  output [31:0] XOR_OUT
);

  xor xor_1 (XOR_OUT[0], DATA_0_IN[0], DATA_1_IN[0]);
  xor xor_2 (XOR_OUT[1], DATA_0_IN[1], DATA_1_IN[1]);
  xor xor_3 (XOR_OUT[2], DATA_0_IN[2], DATA_1_IN[2]);
  xor xor_4 (XOR_OUT[3], DATA_0_IN[3], DATA_1_IN[3]);
  xor xor_5 (XOR_OUT[4], DATA_0_IN[4], DATA_1_IN[4]);
  xor xor_6 (XOR_OUT[5], DATA_0_IN[5], DATA_1_IN[5]);
  xor xor_7 (XOR_OUT[6], DATA_0_IN[6], DATA_1_IN[6]);
  xor xor_8 (XOR_OUT[7], DATA_0_IN[7], DATA_1_IN[7]);
  xor xor_9 (XOR_OUT[8], DATA_0_IN[8], DATA_1_IN[8]);
  xor xor_10 (XOR_OUT[9], DATA_0_IN[9], DATA_1_IN[9]);
  xor xor_11 (XOR_OUT[10], DATA_0_IN[10], DATA_1_IN[10]);
  xor xor_12 (XOR_OUT[11], DATA_0_IN[11], DATA_1_IN[11]);
  xor xor_13 (XOR_OUT[12], DATA_0_IN[12], DATA_1_IN[12]);
  xor xor_14 (XOR_OUT[13], DATA_0_IN[13], DATA_1_IN[13]);
  xor xor_15 (XOR_OUT[14], DATA_0_IN[14], DATA_1_IN[14]);
  xor xor_16 (XOR_OUT[15], DATA_0_IN[15], DATA_1_IN[15]);
  xor xor_17 (XOR_OUT[16], DATA_0_IN[16], DATA_1_IN[16]);
  xor xor_18 (XOR_OUT[17], DATA_0_IN[17], DATA_1_IN[17]);
  xor xor_19 (XOR_OUT[18], DATA_0_IN[18], DATA_1_IN[18]);
  xor xor_20 (XOR_OUT[19], DATA_0_IN[19], DATA_1_IN[19]);
  xor xor_21 (XOR_OUT[20], DATA_0_IN[20], DATA_1_IN[20]);
  xor xor_22 (XOR_OUT[21], DATA_0_IN[21], DATA_1_IN[21]);
  xor xor_23 (XOR_OUT[22], DATA_0_IN[22], DATA_1_IN[22]);
  xor xor_24 (XOR_OUT[23], DATA_0_IN[23], DATA_1_IN[23]);
  xor xor_25 (XOR_OUT[24], DATA_0_IN[24], DATA_1_IN[24]);
  xor xor_26 (XOR_OUT[25], DATA_0_IN[25], DATA_1_IN[25]);
  xor xor_27 (XOR_OUT[26], DATA_0_IN[26], DATA_1_IN[26]);
  xor xor_28 (XOR_OUT[27], DATA_0_IN[27], DATA_1_IN[27]);
  xor xor_29 (XOR_OUT[28], DATA_0_IN[28], DATA_1_IN[28]);
  xor xor_30 (XOR_OUT[29], DATA_0_IN[29], DATA_1_IN[29]);
  xor xor_31 (XOR_OUT[30], DATA_0_IN[30], DATA_1_IN[30]);
  xor xor_32 (XOR_OUT[31], DATA_0_IN[31], DATA_1_IN[31]);
endmodule

// OR
module _32BITS_OR (
  input  [31:0] DATA_0_IN,
  input  [31:0] DATA_1_IN,
  output [31:0] OR_OUT
);

  or or_1 (OR_OUT[0], DATA_0_IN[0], DATA_1_IN[0]);
  or or_2 (OR_OUT[1], DATA_0_IN[1], DATA_1_IN[1]);
  or or_3 (OR_OUT[2], DATA_0_IN[2], DATA_1_IN[2]);
  or or_4 (OR_OUT[3], DATA_0_IN[3], DATA_1_IN[3]);
  or or_5 (OR_OUT[4], DATA_0_IN[4], DATA_1_IN[4]);
  or or_6 (OR_OUT[5], DATA_0_IN[5], DATA_1_IN[5]);
  or or_7 (OR_OUT[6], DATA_0_IN[6], DATA_1_IN[6]);
  or or_8 (OR_OUT[7], DATA_0_IN[7], DATA_1_IN[7]);
  or or_9 (OR_OUT[8], DATA_0_IN[8], DATA_1_IN[8]);
  or or_10 (OR_OUT[9], DATA_0_IN[9], DATA_1_IN[9]);
  or or_11 (OR_OUT[10], DATA_0_IN[10], DATA_1_IN[10]);
  or or_12 (OR_OUT[11], DATA_0_IN[11], DATA_1_IN[11]);
  or or_13 (OR_OUT[12], DATA_0_IN[12], DATA_1_IN[12]);
  or or_14 (OR_OUT[13], DATA_0_IN[13], DATA_1_IN[13]);
  or or_15 (OR_OUT[14], DATA_0_IN[14], DATA_1_IN[14]);
  or or_16 (OR_OUT[15], DATA_0_IN[15], DATA_1_IN[15]);
  or or_17 (OR_OUT[16], DATA_0_IN[16], DATA_1_IN[16]);
  or or_18 (OR_OUT[17], DATA_0_IN[17], DATA_1_IN[17]);
  or or_19 (OR_OUT[18], DATA_0_IN[18], DATA_1_IN[18]);
  or or_20 (OR_OUT[19], DATA_0_IN[19], DATA_1_IN[19]);
  or or_21 (OR_OUT[20], DATA_0_IN[20], DATA_1_IN[20]);
  or or_22 (OR_OUT[21], DATA_0_IN[21], DATA_1_IN[21]);
  or or_23 (OR_OUT[22], DATA_0_IN[22], DATA_1_IN[22]);
  or or_24 (OR_OUT[23], DATA_0_IN[23], DATA_1_IN[23]);
  or or_25 (OR_OUT[24], DATA_0_IN[24], DATA_1_IN[24]);
  or or_26 (OR_OUT[25], DATA_0_IN[25], DATA_1_IN[25]);
  or or_27 (OR_OUT[26], DATA_0_IN[26], DATA_1_IN[26]);
  or or_28 (OR_OUT[27], DATA_0_IN[27], DATA_1_IN[27]);
  or or_29 (OR_OUT[28], DATA_0_IN[28], DATA_1_IN[28]);
  or or_30 (OR_OUT[29], DATA_0_IN[29], DATA_1_IN[29]);
  or or_31 (OR_OUT[30], DATA_0_IN[30], DATA_1_IN[30]);
  or or_32 (OR_OUT[31], DATA_0_IN[31], DATA_1_IN[31]);
endmodule

module _32BITS_OR_SELF (
  input  [31:0] DATA_0_IN,
  output OR_OUT
);

  or or_1 (OR_OUT, DATA_0_IN[0], DATA_0_IN[1], DATA_0_IN[2], DATA_0_IN[3], DATA_0_IN[4], DATA_0_IN[5], DATA_0_IN[6], DATA_0_IN[7], DATA_0_IN[8], DATA_0_IN[9], DATA_0_IN[10], DATA_0_IN[11], DATA_0_IN[12], DATA_0_IN[13], DATA_0_IN[14], DATA_0_IN[15], DATA_0_IN[16], DATA_0_IN[17], DATA_0_IN[18], DATA_0_IN[19], DATA_0_IN[20], DATA_0_IN[21], DATA_0_IN[22], DATA_0_IN[23], DATA_0_IN[24], DATA_0_IN[25], DATA_0_IN[26], DATA_0_IN[27], DATA_0_IN[28], DATA_0_IN[29], DATA_0_IN[30], DATA_0_IN[31]);
endmodule

// REG
module MEM_BANK_EXE_MEM (
  input  [23:0] PC_IN,
  input  [5:0] OPC_IN,
  input  [4:0] RS_IN,
  input  [4:0] RT_IN,
  input  [4:0] RD_IN,
  input  [31:0] ALU_IN,
  input  [31:0] VRT_IN,
  input  FREEZE_IN,
  input  CLOCK_IN,
  input  RESET_IN,
  output [31:0] VRD_OUT,
  output [31:0] VRT_OUT,
  output [23:0] PC_OUT,
  output [5:0] OPC_OUT,
  output [4:0] RS_OUT,
  output [4:0] RT_OUT,
  output [4:0] RD_OUT
);

  wire not_1_out;

  not not_1 (not_1_out, FREEZE_IN);
  Register #(.width(24)) register_1 (.D(PC_IN), .en(not_1_out), .Q(PC_OUT), .clk(CLOCK_IN), .clr(RESET_IN));
  Register #(.width(6)) register_2 (.D(OPC_IN), .en(not_1_out), .Q(OPC_OUT), .clk(CLOCK_IN), .clr(RESET_IN));
  Register #(.width(5)) register_3 (.D(RS_IN), .en(not_1_out), .Q(RS_OUT), .clk(CLOCK_IN), .clr(RESET_IN));
  Register #(.width(5)) register_4 (.D(RT_IN), .en(not_1_out), .Q(RT_OUT), .clk(CLOCK_IN), .clr(RESET_IN));
  Register #(.width(5)) register_5 (.D(RD_IN), .en(not_1_out), .Q(RD_OUT), .clk(CLOCK_IN), .clr(RESET_IN));
  Register #(.width(32)) register_6 (.D(ALU_IN), .en(not_1_out), .Q(VRD_OUT), .clk(CLOCK_IN), .clr(RESET_IN));
  Register #(.width(32)) register_7 (.D(VRT_IN), .en(not_1_out), .Q(VRT_OUT), .clk(CLOCK_IN), .clr(RESET_IN));
endmodule

// MEM
module MEM_STAGE (
  input  [31:0] VRD_IN,
  input  [31:0] VRT_IN,
  input  [23:0] PC_IN,
  input  [5:0] OPC_IN,
  input  FREEZE_IN,
  input  CLOCK_IN,
  input  RESET_IN,
  input  [4:0] RS_IN,
  input  [4:0] RT_IN,
  input  [4:0] RD_IN,
  output ADDR_ERR_OUT,
  output [31:0] VRD_OUT,
  output [23:0] PC_OUT,
  output [5:0] OPC_OUT,
  output [31:0] DATA_OUT,
  output LOAD_OPC_OUT,
  output [4:0] RS_OUT,
  output [4:0] RT_OUT,
  output [4:0] RD_OUT
);

  wire mem_opc_decoder_1_write_out, or_1_out, or_2_out;

  MEM_OPC_DECODER mem_opc_decoder_1 (.OPC_IN(OPC_IN), .LOAD_OUT(LOAD_OPC_OUT), .WRITE_OUT(mem_opc_decoder_1_write_out));
  or or_1 (or_1_out, LOAD_OPC_OUT, mem_opc_decoder_1_write_out);
  or or_2 (or_2_out, ~or_1_out, FREEZE_IN);  // OR_Gate
  RAM_CIRC ram_circ_1 (
    .ADDR_IN(VRD_IN), .DATA_IN(VRT_IN), .WE_IN(mem_opc_decoder_1_write_out), .FREEZE_IN(or_2_out),
    .CLOCK_IN(CLOCK_IN), .RESET_IN(RESET_IN), .ADDR_ERR_OUT(ADDR_ERR_OUT), .DATA_OUT(DATA_OUT));

  assign OPC_OUT = OPC_IN;
  assign PC_OUT = PC_IN;
  assign RD_OUT = RD_IN;
  assign RS_OUT = RS_IN;
  assign RT_OUT = RT_IN;
  assign VRD_OUT = VRD_IN;
endmodule

module RAM_CIRC (
  input  [31:0] ADDR_IN,
  input  [31:0] DATA_IN,
  input  WE_IN,
  input  FREEZE_IN,
  input  CLOCK_IN,
  input  RESET_IN,
  output ADDR_ERR_OUT,
  output [31:0] DATA_OUT
);

  wire and_1_out, comparator_1_lt, not_1_out, not_3_out;
  wire [23:0] bit_extender_1_out;

  Bit_Extender #(.in_width(32), .out_width(24)) bit_extender_1 (.in(ADDR_IN), .out(bit_extender_1_out));
  and and_1 (and_1_out, comparator_1_lt, not_1_out);
  not not_1 (not_1_out, FREEZE_IN);
  not not_2 (ADDR_ERR_OUT, comparator_1_lt);
  Comparator #(.width(32), .mode("unsigned")) comparator_1 (
    .a(ADDR_IN), .b(32'h1000000), .lt(comparator_1_lt));  // open: gt, eq
  RAM #(.addrWidth(24), .dataWidth(32), .bus("separate")) ram_1 (
    .addr(bit_extender_1_out), .din(DATA_IN), .data(DATA_OUT), .str(WE_IN), .sel(and_1_out), .clk(CLOCK_IN),
    .ld(not_3_out), .clr(RESET_IN));
  not not_3 (not_3_out, WE_IN);

  // Notes on the sheet:
  //   MEMORY RANGE SELECT
endmodule

module MEM_OPC_DECODER (
  input  [5:0] OPC_IN,
  output LOAD_OUT,
  output WRITE_OUT
);

  wire comparator_1_eq, comparator_2_eq, comparator_3_eq, comparator_4_eq, comparator_5_eq, comparator_6_eq,
       comparator_7_eq;

  Comparator #(.width(6), .mode("unsigned")) comparator_1 (
    .a(OPC_IN), .b(6'b100011), .eq(comparator_1_eq));  // open: gt, lt
  Comparator #(.width(6), .mode("unsigned")) comparator_2 (
    .a(OPC_IN), .b(6'b100100), .eq(comparator_2_eq));  // open: gt, lt
  Comparator #(.width(6), .mode("unsigned")) comparator_3 (
    .a(OPC_IN), .b(6'b100101), .eq(comparator_3_eq));  // open: gt, lt
  Comparator #(.width(6), .mode("unsigned")) comparator_4 (
    .a(OPC_IN), .b(6'b001111), .eq(comparator_4_eq));  // open: gt, lt
  Comparator #(.width(6), .mode("unsigned")) comparator_5 (
    .a(OPC_IN), .b(6'b101000), .eq(comparator_5_eq));  // open: gt, lt
  Comparator #(.width(6), .mode("unsigned")) comparator_6 (
    .a(OPC_IN), .b(6'b101001), .eq(comparator_6_eq));  // open: gt, lt
  Comparator #(.width(6), .mode("unsigned")) comparator_7 (
    .a(OPC_IN), .b(6'b101011), .eq(comparator_7_eq));  // open: gt, lt
  or or_1 (LOAD_OUT, comparator_1_eq, comparator_2_eq, comparator_3_eq, comparator_4_eq);
  or or_2 (WRITE_OUT, comparator_5_eq, comparator_6_eq, comparator_7_eq);
endmodule

// REG
module MEM_BANK_MEM_WB (
  input  [31:0] VRD_IN,
  input  [23:0] PC_IN,
  input  [5:0] OPC_IN,
  input  [31:0] DATA_IN,
  input  LOAD_OPC_IN,
  input  [4:0] RS_IN,
  input  [4:0] RT_IN,
  input  [4:0] RD_IN,
  input  FREEZE_IN,
  input  CLOCK_IN,
  input  RESET_IN,
  output [31:0] VRD_OUT,
  output [23:0] PC_OUT,
  output [5:0] OPC_OUT,
  output [31:0] DATA_OUT,
  output LOAD_OPC_OUT,
  output [4:0] RS_OUT,
  output [4:0] RT_OUT,
  output [4:0] RD_OUT
);

  wire not_1_out;

  Register #(.width(32)) register_1 (.D(VRD_IN), .en(not_1_out), .Q(VRD_OUT), .clk(CLOCK_IN), .clr(RESET_IN));
  Register #(.width(24)) register_2 (.D(PC_IN), .en(not_1_out), .Q(PC_OUT), .clk(CLOCK_IN), .clr(RESET_IN));
  Register #(.width(6)) register_3 (.D(OPC_IN), .en(not_1_out), .Q(OPC_OUT), .clk(CLOCK_IN), .clr(RESET_IN));
  Register #(.width(32)) register_4 (.D(DATA_IN), .en(not_1_out), .Q(DATA_OUT), .clk(CLOCK_IN), .clr(RESET_IN));
  Register #(.width(1)) register_5 (.D(LOAD_OPC_IN), .en(not_1_out), .Q(LOAD_OPC_OUT), .clk(CLOCK_IN), .clr(RESET_IN));
  Register #(.width(5)) register_6 (.D(RS_IN), .en(not_1_out), .Q(RS_OUT), .clk(CLOCK_IN), .clr(RESET_IN));
  Register #(.width(5)) register_7 (.D(RT_IN), .en(not_1_out), .Q(RT_OUT), .clk(CLOCK_IN), .clr(RESET_IN));
  Register #(.width(5)) register_8 (.D(RD_IN), .en(not_1_out), .Q(RD_OUT), .clk(CLOCK_IN), .clr(RESET_IN));
  not not_1 (not_1_out, FREEZE_IN);
endmodule

// WB
module WB_STAGE (
  input  [31:0] VRD_IN,
  input  [23:0] PC_IN,
  input  [5:0] OPC_IN,
  input  [31:0] DATA_IN,
  input  LOAD_OPC_IN,
  input  [4:0] RS_IN,
  input  [4:0] RT_IN,
  input  [4:0] RD_IN,
  input  FREEZE_IN,
  input  CLOCK_IN,
  input  RESET_IN,
  output [31:0] DATA_OUT,
  output [4:0] DATA_ADDR_OUT
);

  Multiplexer #(.width(32), .disabled(0), .enable("false")) multiplexer_1 (
    .in0(VRD_IN), .in1(DATA_IN), .out(DATA_OUT), .sel(LOAD_OPC_IN));

  assign DATA_ADDR_OUT = RD_IN;
endmodule

module EXE_OPCODE_DEC (
  input  [5:0] ADDR_IN
);
endmodule
