// Logisim project BYPASS_PIPELINE.circ as structural Verilog: 19 circuits, main circuit IF
module IF (
  input  [15:0] PC_IN,
  input  CLOCK_IN,
  output [15:0] plus_1_OUT,
  output [2:0] rC_OUT,
  output [3:0] mid_OUT,
  output [15:0] PC_OUT,
  output [2:0] rB_OUT,
  output [2:0] rA_OUT,
  output [2:0] OP_OUT
);

  ROM #(.addrWidth(16), .dataWidth(16)) rom_1 (
    .addr(PC_OUT), .data({OP_OUT, rA_OUT, rB_OUT, mid_OUT, rC_OUT}));  // open: sel
  Register #(.width(16)) register_1 (.D(PC_IN), .Q(PC_OUT), .clk(CLOCK_IN));  // open: en, clr
  Adder #(.width(16)) adder_1 (.a(PC_OUT), .b(16'h1), .out(plus_1_OUT));  // open: cin, cout

  // Notes on the sheet:
  //   IF STAGE
  //   INSTRUCTION MEM
  //   contents of rom_1 (hex, n*v repeats v):
  //   c385 0 0 ff80 0 0 7401 2405 2804 2c00 5007 2000 a680 aa81 cc87 0 0 1b02 2d81 c07a 0 0 b800 8c00 c002
  //   0 0 9e80 0 1b82 fc00
endmodule

module ID (
  input  [2:0] OP_IN,
  input  [2:0] rA_IN,
  input  [2:0] rB_IN,
  input  [3:0] mid_IN,
  input  [2:0] rC_IN,
  input  WErf_IN,
  input  [2:0] TGTr_IN,
  input  [15:0] PC_IN,
  input  [15:0] TGTd_IN,
  input  CLOCK_IN,
  output [15:0] PC_OUT,
  output [15:0] OPERAND0_OUT,
  output [15:0] OPERAND2_OUT,
  output [15:0] OPERAND1_OUT,
  output [2:0] OP_OUT,
  output [2:0] rT_OUT,
  output [2:0] s1_OUT,
  output [2:0] s2_OUT
);

  wire CTL6_selecmuxop0_out, CTL6_selecmuxs2_out;
  wire [2:0] register_2_q, register_5_q;
  wire [3:0] register_4_q;
  wire [15:0] _43TO7_signedimm_out, _343TO10_imm_out, shifter_1_out;

  Register #(.width(3)) register_1 (.D(OP_IN), .Q(OP_OUT), .clk(CLOCK_IN));  // open: en, clr
  CTL7 CTL7 (.rA_IN(register_2_q), .OP_IN(OP_OUT), .rT_OUT(rT_OUT));
  Register #(.width(3)) register_2 (.D(rA_IN), .Q(register_2_q), .clk(CLOCK_IN));  // open: en, clr
  CTL6 CTL6 (.OP_IN(OP_OUT), .SelecMUXs2_OUT(CTL6_selecmuxs2_out), .SelecMUXop0_OUT(CTL6_selecmuxop0_out));
  Register #(.width(3)) register_3 (.D(rB_IN), .Q(s1_OUT), .clk(CLOCK_IN));  // open: en, clr
  Multiplexer #(.width(3), .enable("false")) multiplexer_1 (
    .in0(register_2_q), .in1(register_5_q), .out(s2_OUT), .sel(CTL6_selecmuxs2_out));
  Register #(.width(4)) register_4 (.D(mid_IN), .Q(register_4_q), .clk(CLOCK_IN));  // open: en, clr
  _343to10 _343TO10 (.rB_IN(s1_OUT), .mid_IN(register_4_q), .rC_IN(register_5_q), .Imm_OUT(_343TO10_imm_out));
  Shifter #(.width(16)) shifter_1 (.in(_343TO10_imm_out), .\dist (4'b0110), .out(shifter_1_out));
  Multiplexer #(.width(16), .enable("false")) multiplexer_2 (
    .in0(shifter_1_out), .in1(_43TO7_signedimm_out), .out(OPERAND0_OUT), .sel(CTL6_selecmuxop0_out));
  _43to7 _43TO7 (.mid_IN(register_4_q), .rC_IN(register_5_q), .SignedImm_OUT(_43TO7_signedimm_out));
  Register #(.width(3)) register_5 (.D(rC_IN), .Q(register_5_q), .clk(CLOCK_IN));  // open: en, clr
  Register #(.width(16)) register_6 (.D(PC_IN), .Q(PC_OUT), .clk(CLOCK_IN));  // open: en, clr
  REGISTER_FILE REGISTER_FILE (
    .CLOCK_IN(WErf_IN), .WErf_IN(CLOCK_IN), .TGTd_IN(TGTd_IN), .TGTr_IN(TGTr_IN), .SRC1d_OUT(OPERAND1_OUT),
    .Src1r_IN(s1_OUT), .SRC2d_OUT(OPERAND2_OUT), .Src2r_IN(s2_OUT));

  // Notes on the sheet:
  //   ID STAGE
  //   MUXs2
  //   MUXop0
endmodule

module REGISTER_FILE (
  input  CLOCK_IN,
  input  WErf_IN,
  input  [2:0] Src1r_IN,
  input  [15:0] TGTd_IN,
  input  [2:0] TGTr_IN,
  input  [2:0] Src2r_IN,
  output [15:0] SRC1d_OUT,
  output [15:0] SRC2d_OUT
);

  wire demultiplexer_1_out1, demultiplexer_1_out2, demultiplexer_1_out3, demultiplexer_1_out4,
       demultiplexer_1_out5, demultiplexer_1_out6, demultiplexer_1_out7;
  wire [15:0] demultiplexer_2_out0, demultiplexer_2_out1, demultiplexer_2_out2, demultiplexer_2_out3,
       demultiplexer_2_out4, demultiplexer_2_out5, demultiplexer_2_out6, demultiplexer_2_out7, r1_q, r2_q,
       r3_q, r4_q, r5_q, r6_q, r7_q;

  Demultiplexer #(.select(3), .enable("false")) demultiplexer_1 (
    .out1(demultiplexer_1_out1), .out2(demultiplexer_1_out2), .out3(demultiplexer_1_out3),
    .out4(demultiplexer_1_out4), .out5(demultiplexer_1_out5), .out6(demultiplexer_1_out6),
    .out7(demultiplexer_1_out7), .in(WErf_IN), .sel(TGTr_IN));  // open: out0
  Demultiplexer #(.select(3), .width(16), .enable("false")) demultiplexer_2 (
    .out0(demultiplexer_2_out0), .out1(demultiplexer_2_out1), .out2(demultiplexer_2_out2),
    .out3(demultiplexer_2_out3), .out4(demultiplexer_2_out4), .out5(demultiplexer_2_out5),
    .out6(demultiplexer_2_out6), .out7(demultiplexer_2_out7), .in(TGTd_IN), .sel(TGTr_IN));
  Register #(.width(16), .trigger("high")) r1 (
    .D(demultiplexer_2_out1), .en(demultiplexer_1_out1), .Q(r1_q), .clk(CLOCK_IN));  // open: clr
  Register #(.width(16), .trigger("high")) r2 (
    .D(demultiplexer_2_out2), .en(demultiplexer_1_out2), .Q(r2_q), .clk(CLOCK_IN));  // open: clr
  Register #(.width(16), .trigger("high")) r3 (
    .D(demultiplexer_2_out3), .en(demultiplexer_1_out3), .Q(r3_q), .clk(CLOCK_IN));  // open: clr
  Register #(.width(16), .trigger("high")) r4 (
    .D(demultiplexer_2_out4), .en(demultiplexer_1_out4), .Q(r4_q), .clk(CLOCK_IN));  // open: clr
  Register #(.width(16), .trigger("high")) r5 (
    .D(demultiplexer_2_out5), .en(demultiplexer_1_out5), .Q(r5_q), .clk(CLOCK_IN));  // open: clr
  Register #(.width(16), .trigger("high")) r6 (
    .D(demultiplexer_2_out6), .en(demultiplexer_1_out6), .Q(r6_q), .clk(CLOCK_IN));  // open: clr
  Register #(.width(16), .trigger("high")) r7 (
    .D(demultiplexer_2_out7), .en(demultiplexer_1_out7), .Q(r7_q), .clk(CLOCK_IN));  // open: clr
  Multiplexer #(.select(3), .width(16), .enable("false")) multiplexer_1 (
    .in0({16{1'b0}}), .in1(r1_q), .in2(r2_q), .in3(r3_q), .in4(r4_q), .in5(r5_q), .in6(r6_q), .in7(r7_q),
    .out(SRC1d_OUT), .sel(Src1r_IN));
  Multiplexer #(.select(3), .width(16), .enable("false")) multiplexer_2 (
    .in0({16{1'b0}}), .in1(r1_q), .in2(r2_q), .in3(r3_q), .in4(r4_q), .in5(r5_q), .in6(r6_q), .in7(r7_q),
    .out(SRC2d_OUT), .sel(Src2r_IN));
  // also tied to GND on the sheet: {demultiplexer_2_out0[0], demultiplexer_2_out0[1], demultiplexer_2_out0[2], demultiplexer_2_out0[3], demultiplexer_2_out0[4], demultiplexer_2_out0[5], demultiplexer_2_out0[6], demultiplexer_2_out0[7], demultiplexer_2_out0[8], demultiplexer_2_out0[9], demultiplexer_2_out0[10], demultiplexer_2_out0[11], demultiplexer_2_out0[12], demultiplexer_2_out0[13], demultiplexer_2_out0[14], demultiplexer_2_out0[15]}

  // Notes on the sheet:
  //   RegisterFile
  //   r0 = 0
endmodule

module CTL7 (
  input  [2:0] rA_IN,
  input  [2:0] OP_IN,
  output [2:0] rT_OUT
);

  wire comparator_1_eq, comparator_2_eq, or_1_out;

  Multiplexer #(.width(3), .enable("false")) multiplexer_1 (.in0(rA_IN), .in1(3'b000), .out(rT_OUT), .sel(or_1_out));
  Comparator #(.width(3), .mode("unsigned")) comparator_1 (
    .a(OP_IN), .b(3'b101), .eq(comparator_1_eq));  // open: gt, lt
  Comparator #(.width(3), .mode("unsigned")) comparator_2 (
    .a(3'b110), .b(OP_IN), .eq(comparator_2_eq));  // open: gt, lt
  or or_1 (or_1_out, comparator_1_eq, comparator_2_eq);

  // Notes on the sheet:
  //   CTL7
  //   SW
  //   BEQ
endmodule

module CTL6 (
  input  [2:0] OP_IN,
  output SelecMUXs2_OUT,
  output SelecMUXop0_OUT
);

  wire comparator_1_eq, comparator_2_eq, comparator_3_eq;

  Comparator #(.width(3), .mode("unsigned")) comparator_1 (
    .a(OP_IN), .b(3'b000), .eq(comparator_1_eq));  // open: gt, lt
  Comparator #(.width(3), .mode("unsigned")) comparator_2 (
    .a(3'b010), .b(OP_IN), .eq(comparator_2_eq));  // open: gt, lt
  Comparator #(.width(3), .mode("unsigned")) comparator_3 (
    .a(OP_IN), .b(3'b011), .eq(comparator_3_eq));  // open: gt, lt
  or or_1 (SelecMUXs2_OUT, comparator_1_eq, comparator_2_eq);
  not not_1 (SelecMUXop0_OUT, comparator_3_eq);

  // Notes on the sheet:
  //   CTL6
  //   ADD
  //   NAND
  //   LUI
endmodule

module _343to10 (
  input  [2:0] rB_IN,
  input  [3:0] mid_IN,
  input  [2:0] rC_IN,
  output [15:0] Imm_OUT
);


  assign Imm_OUT = {{6{1'b0}}, rB_IN, mid_IN, rC_IN};

  // Notes on the sheet:
  //   343to10
  //   Reconstituter Imm depuis rB mid rC
endmodule

module _43to7 (
  input  [3:0] mid_IN,
  input  [2:0] rC_IN,
  output [15:0] SignedImm_OUT
);


  assign SignedImm_OUT = {{9{1'b0}}, mid_IN, rC_IN};

  // Notes on the sheet:
  //   43to7
  //   Reconstituter Signed Imm depuis mid et rC
endmodule

// EXE
module EX (
  input  [2:0] OP_IN,
  input  [2:0] rT_IN,
  input  [2:0] s1_IN,
  input  [2:0] s2_IN,
  input  [15:0] PC_IN,
  input  [15:0] OPERAND0_IN,
  input  [15:0] OPERAND2_IN,
  input  [15:0] OPERAND1_IN,
  input  CLOCK_IN,
  input  [15:0] RF_WRITE_DATA2_IN,
  input  [2:0] rT1_IN,
  input  [2:0] rT2_IN,
  input  [15:0] RF_WRITE_DATA1_IN,
  input  [2:0] rT3_IN,
  input  [15:0] MEM_ALU_OUTPUT_IN,
  output [15:0] MUXalu1_OUT,
  output [1:0] MUXpc_OUT,
  output [15:0] PC___1___OPERAND0_OUT,
  output [15:0] PC_OUT,
  output [15:0] STORE_DATA_OUT,
  output [15:0] ALU_OUTPUT_OUT,
  output [2:0] OP_OUT,
  output [2:0] rT_OUT
);

  wire alu_1_eq__out;
  wire [1:0] ctl3_1_funcalu_out, ctl4_1_muximm_out, CTL5_muxalu1, CTL5_muxalu2;
  wire [2:0] register_3_q, register_4_q;
  wire [15:0] adder_1_out, multiplexer_3_out, register_6_q, register_7_q, register_8_q;

  Register #(.width(3)) register_1 (.D(OP_IN), .Q(OP_OUT), .clk(CLOCK_IN));  // open: en, clr
  Register #(.width(3)) register_2 (.D(rT_IN), .Q(rT_OUT), .clk(CLOCK_IN));  // open: en, clr
  CTL5 CTL5 (
    .rT1(rT1_IN), .rT2(rT2_IN), .rT3(rT3_IN), .s1(register_3_q), .s2(register_4_q), .MUXalu2(CTL5_muxalu2),
    .MUXalu1(CTL5_muxalu1));
  CTL4 ctl4_1 (.OP_IN(OP_OUT), .MUXimm_OUT(ctl4_1_muximm_out));
  CTL3 ctl3_1 (.OP_IN(OP_OUT), .MUXpc_OUT(MUXpc_OUT), .FUNCalu_OUT(ctl3_1_funcalu_out), .EQ__IN(alu_1_eq__out));
  Register #(.width(3)) register_3 (.D(s1_IN), .Q(register_3_q), .clk(CLOCK_IN));  // open: en, clr
  Register #(.width(3)) register_4 (.D(s2_IN), .Q(register_4_q), .clk(CLOCK_IN));  // open: en, clr
  Register #(.width(16)) register_5 (.D(PC_IN), .Q(PC_OUT), .clk(CLOCK_IN));  // open: en, clr
  Register #(.width(16)) register_6 (.D(OPERAND0_IN), .Q(register_6_q), .clk(CLOCK_IN));  // open: en, clr
  Adder #(.width(16)) adder_1 (.a(PC_OUT), .b(16'h1), .out(adder_1_out));  // open: cin, cout
  ADD7BITSIGNED add7bitsigned_1 (
    .PC_1_IN(adder_1_out), .OPERAND0_IN(register_6_q), .PC_1_OPERAND0_OUT(PC___1___OPERAND0_OUT));
  Register #(.width(16)) register_7 (.D(OPERAND2_IN), .Q(register_7_q), .clk(CLOCK_IN));  // open: en, clr
  Multiplexer #(.select(2), .width(16), .enable("false")) multiplexer_1 (
    .in0(register_7_q), .in1(RF_WRITE_DATA2_IN), .in2(RF_WRITE_DATA1_IN), .in3(MEM_ALU_OUTPUT_IN),
    .out(STORE_DATA_OUT), .sel(CTL5_muxalu2));
  Register #(.width(16)) register_8 (.D(OPERAND1_IN), .Q(register_8_q), .clk(CLOCK_IN));  // open: en, clr
  Multiplexer #(.select(2), .width(16), .enable("false")) multiplexer_2 (
    .in0(MEM_ALU_OUTPUT_IN), .in1(RF_WRITE_DATA1_IN), .in2(RF_WRITE_DATA2_IN), .in3(register_8_q),
    .out(MUXalu1_OUT), .sel(CTL5_muxalu1));
  Multiplexer #(.select(2), .width(16), .enable("false")) multiplexer_3 (
    .in0(register_6_q), .in1(adder_1_out), .in2(STORE_DATA_OUT), .out(multiplexer_3_out),
    .sel(ctl4_1_muximm_out));  // open: in3
  ALU alu_1 (
    .FUNCalu_IN(ctl3_1_funcalu_out), .EQ__OUT(alu_1_eq__out), .SRC2_IN(multiplexer_3_out),
    .SRC1_IN(MUXalu1_OUT), .ALU_OUT(ALU_OUTPUT_OUT));

  // Notes on the sheet:
  //   EX
  //   CTL4
  //   CTL3
  //   PC + 1
  //   ADD PC + 1 + OPERAND0
  //   ALU
endmodule

module CTL3 (
  input  [2:0] OP_IN,
  input  EQ__IN,
  output [1:0] MUXpc_OUT,
  output [1:0] FUNCalu_OUT
);

  wire comparator_1_eq, comparator_3_eq, comparator_4_eq, comparator_5_eq, nand_1_out, not_1_out;

  Comparator #(.width(3), .mode("unsigned")) comparator_1 (
    .a(OP_IN), .b(3'b110), .eq(comparator_1_eq));  // open: gt, lt
  Comparator #(.width(3), .mode("unsigned")) comparator_2 (.a(OP_IN), .b(3'b111), .eq(MUXpc_OUT[0]));  // open: gt, lt
  and and_1 (MUXpc_OUT[1], nand_1_out, not_1_out);
  not not_1 (not_1_out, MUXpc_OUT[0]);
  nand nand_1 (nand_1_out, comparator_1_eq, EQ__IN);
  Comparator #(.width(3), .mode("unsigned")) comparator_3 (
    .a(OP_IN), .b(3'b000), .eq(comparator_3_eq));  // open: gt, lt
  or or_1 (FUNCalu_OUT[1], comparator_4_eq, comparator_5_eq);
  Comparator #(.width(3), .mode("unsigned")) comparator_4 (
    .a(OP_IN), .b(3'b010), .eq(comparator_4_eq));  // open: gt, lt
  Comparator #(.width(3), .mode("unsigned")) comparator_5 (
    .a(OP_IN), .b(3'b011), .eq(comparator_5_eq));  // open: gt, lt
  or or_2 (FUNCalu_OUT[0], comparator_3_eq, comparator_5_eq);

  // Notes on the sheet:
  //   CTL3
  //   OP == BEQ?
  //   OP == JALR?
endmodule

module ALU (
  input  [15:0] SRC2_IN,
  input  [15:0] SRC1_IN,
  input  [1:0] FUNCalu_IN,
  output [15:0] ALU_OUT,
  output EQ__OUT
);

  wire [15:0] ADD7BITSIGNED_pc_1_operand0_out, adder_1_out, nand_1_out;

  ADD7BITSIGNED ADD7BITSIGNED (
    .PC_1_IN(SRC1_IN), .OPERAND0_IN(SRC2_IN), .PC_1_OPERAND0_OUT(ADD7BITSIGNED_pc_1_operand0_out));
  Comparator #(.width(16), .mode("unsigned")) comparator_1 (.a(SRC1_IN), .b(SRC2_IN), .eq(EQ__OUT));  // open: gt, lt
  assign nand_1_out = ~(SRC2_IN & SRC1_IN);  // NAND_Gate nand_1, 16 bits wide
  Adder #(.width(16)) adder_1 (.a(SRC1_IN), .b(SRC2_IN), .out(adder_1_out));  // open: cin, cout
  Multiplexer #(.select(2), .width(16), .enable("false")) multiplexer_1 (
    .in0(ADD7BITSIGNED_pc_1_operand0_out), .in1(adder_1_out), .in2(nand_1_out), .in3(SRC2_IN), .out(ALU_OUT),
    .sel(FUNCalu_IN));

  // Notes on the sheet:
  //   ALU
  //   EQ ? : SRC2 == SRC1 ?
  //   NAND
  //   ADD
  //   FUNCalu
endmodule

module CTL4 (
  input  [2:0] OP_IN,
  output [1:0] MUXimm_OUT
);

  wire comparator_2_eq, comparator_3_eq, comparator_4_eq;

  Comparator #(.width(3), .mode("unsigned")) comparator_1 (.a(OP_IN), .b(3'b111), .eq(MUXimm_OUT[0]));  // open: gt, lt
  Comparator #(.width(3), .mode("unsigned")) comparator_2 (
    .a(OP_IN), .b(3'b000), .eq(comparator_2_eq));  // open: gt, lt
  Comparator #(.width(3), .mode("unsigned")) comparator_3 (
    .a(OP_IN), .b(3'b010), .eq(comparator_3_eq));  // open: gt, lt
  Comparator #(.width(3), .mode("unsigned")) comparator_4 (
    .a(OP_IN), .b(3'b110), .eq(comparator_4_eq));  // open: gt, lt
  or or_1 (MUXimm_OUT[1], comparator_2_eq, comparator_3_eq, comparator_4_eq);

  // Notes on the sheet:
  //   CTL4
  //   OP == JALR?
  //   OP == ADD?
  //   OP == NAND?
  //   OP == BEQ?
endmodule

module MEM (
  input  [2:0] OP_IN,
  input  [2:0] rT_IN,
  input  [15:0] PC_IN,
  input  [15:0] STORE_DATA_IN,
  input  [15:0] ALU_OUTPUT_IN,
  input  CLOCK_IN,
  output [15:0] ALU_OUTPUT_OUT,
  output [2:0] rT1__to_CTL5__OUT,
  output [15:0] RF_WRITE_DATA_OUT,
  output [2:0] rT_OUT
);

  wire ctl2_1_muxout_out, ctl2_1_wedmem_out;
  wire [2:0] register_1_q;
  wire [15:0] ram_1_data, register_3_q, register_4_q;

  Register #(.width(3)) register_1 (.D(OP_IN), .Q(register_1_q), .clk(CLOCK_IN));  // open: en, clr
  Register #(.width(3)) register_2 (.D(rT_IN), .Q(rT1__to_CTL5__OUT), .clk(CLOCK_IN));  // open: en, clr
  CTL2 ctl2_1 (.OP_IN(register_1_q), .WEdmem_OUT(ctl2_1_wedmem_out), .MUXout_OUT(ctl2_1_muxout_out));
  Register #(.width(16)) register_3 (.D(PC_IN), .Q(register_3_q), .clk(CLOCK_IN));  // open: en, clr
  Register #(.width(16)) register_4 (.D(STORE_DATA_IN), .Q(register_4_q), .clk(CLOCK_IN));  // open: en, clr
  Multiplexer #(.width(16), .enable("false")) multiplexer_1 (
    .in0(ALU_OUTPUT_OUT), .in1(ram_1_data), .out(RF_WRITE_DATA_OUT), .sel(ctl2_1_muxout_out));
  Register #(.width(16)) register_5 (.D(ALU_OUTPUT_IN), .Q(ALU_OUTPUT_OUT), .clk(CLOCK_IN));  // open: en, clr
  RAM #(.addrWidth(16), .dataWidth(16), .bus("separate")) ram_1 (
    .addr(ALU_OUTPUT_OUT), .din(register_4_q), .data(ram_1_data), .str(ctl2_1_wedmem_out), .clk(CLOCK_IN));  // open: sel, ld, clr

  assign rT_OUT = rT1__to_CTL5__OUT;

  // Notes on the sheet:
  //   MEM
  //   CTL2
  //   UNUSED
  //   END PC PIPE
  //   DATA MEMORY
endmodule

module CTL2 (
  input  [2:0] OP_IN,
  output WEdmem_OUT,
  output MUXout_OUT
);

  Comparator #(.width(3), .mode("unsigned")) comparator_1 (.a(OP_IN), .b(3'b101), .eq(WEdmem_OUT));  // open: gt, lt
  Comparator #(.width(3), .mode("unsigned")) comparator_2 (.a(OP_IN), .b(3'b100), .eq(MUXout_OUT));  // open: gt, lt

  // Notes on the sheet:
  //   CTL2
  //   OP == SW?
  //   OP == LW?
endmodule

module WB (
  input  [2:0] rT_IN,
  input  [15:0] RF_WRITE_DATA_IN,
  input  CLOCK_IN,
  output WErf_OUT,
  output [15:0] RF_WRITE_DATA1_OUT,
  output [2:0] rT2__to_CTL5__OUT,
  output [2:0] rT3__to_CTL5__OUT,
  output [15:0] RF_WRITE_DATA2_OUT,
  output [2:0] rT_OUT
);

  Register #(.width(3)) register_1 (.D(rT_IN), .Q(rT2__to_CTL5__OUT), .clk(CLOCK_IN));  // open: en, clr
  Register #(.width(3)) register_2 (.D(rT2__to_CTL5__OUT), .Q(rT3__to_CTL5__OUT), .clk(CLOCK_IN));  // open: en, clr
  Register #(.width(16)) register_3 (.D(RF_WRITE_DATA_IN), .Q(RF_WRITE_DATA1_OUT), .clk(CLOCK_IN));  // open: en, clr
  CTL1 ctl1_1 (.rT_IN(rT2__to_CTL5__OUT), .WErf_OUT(WErf_OUT));
  Register #(.width(16)) register_4 (.D(RF_WRITE_DATA1_OUT), .Q(RF_WRITE_DATA2_OUT), .clk(CLOCK_IN));  // open: en, clr

  assign rT_OUT = rT2__to_CTL5__OUT;

  // Notes on the sheet:
  //   WB
  //   CTL1
endmodule

module CTL1 (
  input  [2:0] rT_IN,
  output WErf_OUT
);

  wire comparator_1_eq;

  not not_1 (WErf_OUT, comparator_1_eq);
  Comparator #(.width(3), .mode("unsigned")) comparator_1 (
    .a(rT_IN), .b(3'b000), .eq(comparator_1_eq));  // open: gt, lt

  // Notes on the sheet:
  //   CTL1
  //   rT IN == 000 ?
endmodule

module ADD7BITSIGNED (
  input  [15:0] PC_1_IN,
  input  [15:0] OPERAND0_IN,
  output [15:0] PC_1_OPERAND0_OUT
);

  wire comparator_1_gt;
  wire [15:0] adder_1_out, adder_2_out, and_1_out, subtractor_1_out;

  Adder #(.width(16)) adder_1 (.a(PC_1_IN), .b(OPERAND0_IN), .out(adder_1_out));  // open: cin, cout
  Comparator #(.width(16)) comparator_1 (.a(OPERAND0_IN), .b(16'h3f), .gt(comparator_1_gt));  // open: eq, lt
  assign and_1_out = ~OPERAND0_IN & 16'h7f;  // AND_Gate and_1, 16 bits wide
  Adder #(.width(16)) adder_2 (.a(and_1_out), .b(16'h1), .out(adder_2_out));  // open: cin, cout
  Subtractor #(.width(16)) subtractor_1 (.a(PC_1_IN), .b(adder_2_out), .out(subtractor_1_out));  // open: bin, bout
  Multiplexer #(.width(16), .enable("false")) multiplexer_1 (
    .in0(adder_1_out), .in1(subtractor_1_out), .out(PC_1_OPERAND0_OUT), .sel(comparator_1_gt));

  // Notes on the sheet:
  //   ADD SIGNED
endmodule

module CTL5 (
  input  [2:0] s1,
  input  [2:0] s2,
  input  [2:0] rT1,
  input  [2:0] rT2,
  input  [2:0] rT3,
  output [1:0] MUXalu2,
  output [1:0] MUXalu1
);

  wire comparator_1_eq, comparator_2_eq, comparator_3_eq, comparator_4_eq, comparator_5_eq, comparator_6_eq,
       comparator_7_eq, comparator_8_eq, not_1_out, not_2_out, out_selector_1_out0, out_selector_1_out1,
       out_selector_2_out0, out_selector_2_out1;

  Comparator #(.width(3), .mode("unsigned")) comparator_1 (.a(s1), .b(3'b000), .eq(comparator_1_eq));  // open: gt, lt
  Comparator #(.width(3)) comparator_2 (.a(s1), .b(rT1), .eq(comparator_2_eq));  // open: gt, lt
  Comparator #(.width(3)) comparator_3 (.a(s1), .b(rT2), .eq(comparator_3_eq));  // open: gt, lt
  Comparator #(.width(3)) comparator_4 (.a(s1), .b(rT3), .eq(comparator_4_eq));  // open: gt, lt
  not not_1 (not_1_out, comparator_1_eq);
  OUT_SELECTOR out_selector_1 (
    .rT1(comparator_2_eq), .rT2(comparator_3_eq), .rT3(comparator_4_eq), .ENABLE_IN(not_1_out),
    .OUT0(out_selector_1_out0), .OUT1(out_selector_1_out1));
  Comparator #(.width(3)) comparator_5 (.a(s2), .b(rT1), .eq(comparator_5_eq));  // open: gt, lt
  Comparator #(.width(3)) comparator_6 (.a(s2), .b(rT2), .eq(comparator_6_eq));  // open: gt, lt
  Comparator #(.width(3)) comparator_7 (.a(s2), .b(rT3), .eq(comparator_7_eq));  // open: gt, lt
  not not_2 (not_2_out, comparator_8_eq);
  Comparator #(.width(3), .mode("unsigned")) comparator_8 (.a(s2), .b(3'b000), .eq(comparator_8_eq));  // open: gt, lt
  or or_1 (MUXalu1[0], comparator_1_eq, out_selector_1_out0);
  or or_2 (MUXalu1[1], comparator_1_eq, out_selector_1_out1);
  OUT_SELECTOR out_selector_2 (
    .rT1(comparator_5_eq), .rT2(comparator_6_eq), .rT3(comparator_7_eq), .ENABLE_IN(not_2_out),
    .OUT0(out_selector_2_out0), .OUT1(out_selector_2_out1));
  and and_1 (MUXalu2[0], not_2_out, ~out_selector_2_out0);  // AND_Gate
  and and_2 (MUXalu2[1], not_2_out, ~out_selector_2_out1);  // AND_Gate
endmodule

module OUT_SELECTOR (
  input  ENABLE_IN,
  input  rT1,
  input  rT2,
  input  rT3,
  output OUT0,
  output OUT1
);

  wire and_1_out, and_2_out, and_3_out, and_4_out, or_1_out, or_2_out;

  and and_1 (and_1_out, ~rT1, ~rT2, ~rT3);  // AND_Gate
  and and_2 (and_2_out, ~rT1, ~rT2, rT3);  // AND_Gate
  and and_3 (and_3_out, ~rT1, rT2, rT3);  // AND_Gate
  and and_4 (and_4_out, ~rT1, rT2, ~rT3);  // AND_Gate
  or or_1 (or_1_out, and_1_out, and_2_out);
  or or_2 (or_2_out, and_1_out, and_3_out, and_4_out);
  and and_5 (OUT0, ENABLE_IN, or_2_out);
  and and_6 (OUT1, or_1_out, ENABLE_IN);
endmodule

module BYPASS_PIPELINE (
);

  wire CLOCK_out, wb_1_werf_out;
  wire [1:0] ex_1_muxpc_out;
  wire [2:0] ex_1_op_out, ex_1_rt_out, id_1_op_out, id_1_rt_out, id_1_s1_out, id_1_s2_out, if_1_op_out,
       if_1_ra_out, if_1_rb_out, if_1_rc_out, mem_1_rt1__to_ctl5__out, mem_1_rt_out, wb_1_rt2__to_ctl5__out,
       wb_1_rt3__to_ctl5__out, wb_1_rt_out;
  wire [3:0] if_1_mid_out;
  wire [15:0] ex_1_alu_output_out, ex_1_muxalu1_out, ex_1_pc___1___operand0_out, ex_1_pc_out,
       ex_1_store_data_out, id_1_operand0_out, id_1_operand1_out, id_1_operand2_out, id_1_pc_out,
       if_1_pc_out, if_1_plus_1_out, mem_1_alu_output_out, mem_1_rf_write_data_out, multiplexer_1_out,
       wb_1_rf_write_data1_out, wb_1_rf_write_data2_out;

  Clock CLOCK (.out(CLOCK_out));
  ID id_1 (
    .CLOCK_IN(CLOCK_out), .OP_IN(if_1_op_out), .rA_IN(if_1_ra_out), .rB_IN(if_1_rb_out),
    .mid_IN(if_1_mid_out), .rC_IN(if_1_rc_out), .PC_IN(if_1_pc_out), .WErf_IN(wb_1_werf_out),
    .TGTr_IN(wb_1_rt_out), .TGTd_IN(wb_1_rf_write_data1_out), .OP_OUT(id_1_op_out), .rT_OUT(id_1_rt_out),
    .s1_OUT(id_1_s1_out), .s2_OUT(id_1_s2_out), .PC_OUT(id_1_pc_out), .OPERAND0_OUT(id_1_operand0_out),
    .OPERAND2_OUT(id_1_operand2_out), .OPERAND1_OUT(id_1_operand1_out));
  Multiplexer #(.select(2), .width(16), .enable("false")) multiplexer_1 (
    .in0(ex_1_pc___1___operand0_out), .in1(ex_1_muxalu1_out), .in2(if_1_plus_1_out), .out(multiplexer_1_out),
    .sel(ex_1_muxpc_out));  // open: in3
  IF if_1 (
    .CLOCK_IN(CLOCK_out), .PC_IN(multiplexer_1_out), .OP_OUT(if_1_op_out), .rA_OUT(if_1_ra_out),
    .rB_OUT(if_1_rb_out), .mid_OUT(if_1_mid_out), .rC_OUT(if_1_rc_out), .PC_OUT(if_1_pc_out),
    .plus_1_OUT(if_1_plus_1_out));
  EX ex_1 (
    .CLOCK_IN(CLOCK_out), .rT1_IN(mem_1_rt1__to_ctl5__out), .rT2_IN(wb_1_rt2__to_ctl5__out),
    .rT3_IN(wb_1_rt3__to_ctl5__out), .MUXpc_OUT(ex_1_muxpc_out),
    .PC___1___OPERAND0_OUT(ex_1_pc___1___operand0_out), .OP_IN(id_1_op_out), .rT_IN(id_1_rt_out),
    .s1_IN(id_1_s1_out), .s2_IN(id_1_s2_out), .PC_IN(id_1_pc_out), .OPERAND0_IN(id_1_operand0_out),
    .OPERAND2_IN(id_1_operand2_out), .OPERAND1_IN(id_1_operand1_out), .MUXalu1_OUT(ex_1_muxalu1_out),
    .OP_OUT(ex_1_op_out), .rT_OUT(ex_1_rt_out), .PC_OUT(ex_1_pc_out), .STORE_DATA_OUT(ex_1_store_data_out),
    .ALU_OUTPUT_OUT(ex_1_alu_output_out), .RF_WRITE_DATA2_IN(wb_1_rf_write_data2_out),
    .RF_WRITE_DATA1_IN(wb_1_rf_write_data1_out), .MEM_ALU_OUTPUT_IN(mem_1_alu_output_out));
  MEM mem_1 (
    .CLOCK_IN(CLOCK_out), .rT1__to_CTL5__OUT(mem_1_rt1__to_ctl5__out), .OP_IN(ex_1_op_out),
    .rT_IN(ex_1_rt_out), .PC_IN(ex_1_pc_out), .STORE_DATA_IN(ex_1_store_data_out),
    .ALU_OUTPUT_IN(ex_1_alu_output_out), .rT_OUT(mem_1_rt_out), .RF_WRITE_DATA_OUT(mem_1_rf_write_data_out),
    .ALU_OUTPUT_OUT(mem_1_alu_output_out));
  WB wb_1 (
    .CLOCK_IN(CLOCK_out), .rT2__to_CTL5__OUT(wb_1_rt2__to_ctl5__out),
    .rT3__to_CTL5__OUT(wb_1_rt3__to_ctl5__out), .rT_IN(mem_1_rt_out),
    .RF_WRITE_DATA_IN(mem_1_rf_write_data_out), .WErf_OUT(wb_1_werf_out), .rT_OUT(wb_1_rt_out),
    .RF_WRITE_DATA2_OUT(wb_1_rf_write_data2_out), .RF_WRITE_DATA1_OUT(wb_1_rf_write_data1_out));

  // Notes on the sheet:
  //   BYPASS PIPELINE RiSC 16
endmodule
